// Logisim project 4symbol_compara.circ as structural Verilog: 3 circuits, main circuit 1bit_compara
module _1bit_compara (
  input  A,
  input  B,
  output OUT,
  output Equal
);

  wire not_1_out;

  not not_1 (not_1_out, B);
  and and_1 (OUT, A, not_1_out);
  xnor xnor_1 (Equal, A, B);
endmodule

module SYMBOL (
  input  A,
  input  B,
  output OUT,
  output Equal,
  output [1:0] AB
);

  wire not_1_out;

  not not_1 (not_1_out, B);
  and and_1 (OUT, A, not_1_out);
  xnor xnor_1 (Equal, A, B);

  assign AB = {A, B};
endmodule

module _4bit_compara (
  input  [3:0] A,
  input  [3:0] B,
  output OUT
);

  wire _00_11_out, _0_out, _1_equal, _01_out, _1_out, _2_equal, _2_out, _10_out, and_1_out, and_2_out,
       not_1_out, not_2_out, not_3_out, not_4_out, or_out, SYMBOL_equal, SYMBOL_out;
  wire [1:0] SYMBOL_ab;

  SYMBOL SYMBOL (.A(A[3]), .B(B[3]), .OUT(SYMBOL_out), .Equal(SYMBOL_equal), .AB(SYMBOL_ab));
  _1bit_compara _2 (.A(A[2]), .B(B[2]), .OUT(_2_out), .Equal(_2_equal));
  _1bit_compara _1 (.A(A[1]), .B(B[1]), .OUT(_1_out), .Equal(_1_equal));
  _1bit_compara _0 (.A(A[0]), .B(B[0]), .OUT(_0_out));  // open: Equal
  and and_1 (and_1_out, _2_equal, _1_out);
  and and_2 (and_2_out, _2_equal, _1_equal, _0_out);
  not not_1 (not_1_out, SYMBOL_out);
  or \or  (or_out, _2_out, and_1_out, and_2_out);
  not not_2 (not_2_out, SYMBOL_equal);
  and _01 (_01_out, not_2_out, not_3_out);
  not not_3 (not_3_out, SYMBOL_out);
  and _10 (_10_out, not_4_out, SYMBOL_equal);
  not not_4 (not_4_out, SYMBOL_out);
  and _00_11 (_00_11_out, not_1_out, SYMBOL_equal, or_out);
  Multiplexer #(.select(2), .enable("false")) multiplexer_1 (
    .in0(_00_11_out), .in1(_01_out), .in2(_10_out), .in3(_00_11_out), .out(OUT), .sel(SYMBOL_ab));
endmodule
