// Logisim project alu.circ as structural Verilog: 5 circuits, main circuit add
module add (
  input  [3:0] A,
  input  [3:0] B,
  output [3:0] C
);

  Adder #(.width(4)) adder_1 (.a(A), .b(B), .out(C));  // open: cin, cout
endmodule

module sub (
  input  [3:0] A,
  input  [3:0] B,
  output [3:0] C
);

  Subtractor #(.width(4)) subtractor_1 (.a(A), .b(B), .out(C));  // open: bin, bout
endmodule

module AND (
  input  [3:0] A,
  input  [3:0] B,
  output [3:0] C
);

  and _0 (C[0], A[0], B[0]);
  and _1 (C[1], A[1], B[1]);
  and _2 (C[2], A[2], B[2]);
  and _3 (C[3], A[3], B[3]);
endmodule

module OR (
  input  [3:0] A,
  input  [3:0] B,
  output [3:0] C
);

  or _0 (C[0], A[0], B[0]);
  or _3 (C[3], A[3], B[3]);
  or _1 (C[1], A[1], B[1]);
  or _2 (C[2], A[2], B[2]);
endmodule

module alu (
  input  [3:0] A,
  input  [3:0] B,
  input  [1:0] ALUOp,
  output [3:0] C
);

  wire [3:0] add_1_c, and_1_c, or_1_c, sub_1_c;

  add add_1 (.A(A), .B(B), .C(add_1_c));
  sub sub_1 (.A(A), .B(B), .C(sub_1_c));
  AND and_1 (.A(A), .B(B), .C(and_1_c));
  OR or_1 (.A(A), .B(B), .C(or_1_c));
  Multiplexer #(.select(2), .width(4), .enable("false")) multiplexer_1 (
    .in0(add_1_c), .in1(sub_1_c), .in2(and_1_c), .in3(or_1_c), .out(C), .sel(ALUOp));
endmodule
