// Logisim project alu6.circ as structural Verilog
module add (
  input  [3:0] a,
  input  [3:0] b,
  output [3:0] out_3
);

  Adder #(.width(4)) adder_1 (.a(a), .b(b), .out(out_3));  // open: cin, cout
endmodule

module sub (
  input  [3:0] a,
  input  [3:0] b,
  output [3:0] out_3
);

  Subtractor #(.width(4)) subtractor_1 (.a(a), .b(b), .out(out_3));  // open: bin, bout
endmodule

module \and  (
  input  [3:0] a,
  input  [3:0] b,
  output [3:0] out_3
);

  assign out_3 = a & b;  // AND_Gate and_1, 4 bits wide
endmodule
