// Logisim project comparator.circ as structural Verilog: 2 circuits, main circuit compara_1
module compara_1 (
  input  A,
  input  B,
  output Out,
  output equal
);

  wire not_1_out;

  not not_1 (not_1_out, B);
  and and_1 (Out, A, not_1_out);
  xnor xnor_1 (equal, A, B);
endmodule

module comparator (
  input  [3:0] A,
  input  [3:0] B,
  output Out
);

  wire _0_out, _1_equal, _1_out, _2_equal, _2_out, _3_equal, _3_out, and_1_out, and_2_out, and_3_out;

  compara_1 _3 (.A(A[3]), .B(B[3]), .Out(_3_out), .equal(_3_equal));
  compara_1 _2 (.A(A[2]), .B(B[2]), .Out(_2_out), .equal(_2_equal));
  compara_1 _1 (.A(A[1]), .B(B[1]), .Out(_1_out), .equal(_1_equal));
  and and_1 (and_1_out, _3_equal, _2_equal, _1_out);
  compara_1 _0 (.A(A[0]), .B(B[0]), .Out(_0_out));  // open: equal
  and and_2 (and_2_out, _3_equal, _2_out);
  and and_3 (and_3_out, _3_equal, _2_equal, _1_equal, _0_out);
  or or_1 (Out, _3_out, and_2_out, and_1_out, and_3_out);
endmodule
