// Logisim project comparator_ly.circ as structural Verilog: 7 circuits, main circuit main
module main (
  input  A,
  input  B,
  output F1,
  output F2,
  output F3
);

  wire and_3_out, and_4_out, nand_1_out, nand_2_out, nand_3_out, nand_4_out;

  nand nand_1 (nand_1_out, A, B);
  nand nand_2 (nand_2_out, A, B);
  nand nand_3 (nand_3_out, A, B);
  nand nand_4 (nand_4_out, A, B);
  and and_1 (F1, A, nand_1_out);
  and and_2 (F2, B, nand_2_out);
  and and_3 (and_3_out, A, nand_3_out);
  and and_4 (and_4_out, B, nand_4_out);
  nor nor_1 (F3, and_3_out, and_4_out);
endmodule

module _1bit_comparator (
  input  A,
  input  B,
  output F1,
  output F2,
  output F3
);

  wire nand_1_out;

  and and_1 (F1, A, nand_1_out);
  nand nand_1 (nand_1_out, A, B);
  and and_2 (F3, nand_1_out, B);
  nor nor_1 (F2, F1, F3);
endmodule

module comparator (
  input  [3:0] A,
  input  [3:0] B,
  output Out
);

  wire and_1_out, and_2_out, and_3_out, n1bit_comparator_1_f1, n1bit_comparator_1_f2, n1bit_comparator_2_f1,
       n1bit_comparator_2_f2, n1bit_comparator_3_f1, n1bit_comparator_3_f2, n1bit_comparator_4_f1;

  _1bit_comparator u_1bit_comparator_1 (
    .A(A[3]), .B(B[3]), .F1(n1bit_comparator_1_f1), .F2(n1bit_comparator_1_f2));  // open: F3
  _1bit_comparator u_1bit_comparator_2 (
    .A(A[2]), .B(B[2]), .F1(n1bit_comparator_2_f1), .F2(n1bit_comparator_2_f2));  // open: F3
  _1bit_comparator u_1bit_comparator_3 (
    .A(A[1]), .B(B[1]), .F1(n1bit_comparator_3_f1), .F2(n1bit_comparator_3_f2));  // open: F3
  _1bit_comparator u_1bit_comparator_4 (.A(A[0]), .B(B[0]), .F1(n1bit_comparator_4_f1));  // open: F2, F3
  and and_1 (and_1_out, n1bit_comparator_1_f2, n1bit_comparator_2_f1);
  and and_2 (and_2_out, n1bit_comparator_1_f2, n1bit_comparator_2_f2, n1bit_comparator_3_f1);
  and and_3 (and_3_out, n1bit_comparator_1_f2, n1bit_comparator_2_f2, n1bit_comparator_3_f2, n1bit_comparator_4_f1);
  or or_1 (Out, n1bit_comparator_1_f1, and_1_out, and_2_out, and_3_out);
endmodule

module _1bit_cmp (
  input  A,
  input  B,
  output H,
  output E,
  output L
);

  and and_1 (H, A, ~B);  // AND_Gate
  xnor xnor_1 (E, A, B);
  and and_2 (L, ~A, B);  // AND_Gate
endmodule

module _4bit_cmp (
  input  [3:0] A,
  input  [3:0] B,
  output Out
);

  wire and_1_out, and_2_out, and_3_out, n1bit_cmp_1_e, n1bit_cmp_1_h, n1bit_cmp_2_e, n1bit_cmp_2_h,
       n1bit_cmp_3_e, n1bit_cmp_3_h, n1bit_cmp_4_h;

  _1bit_cmp u_1bit_cmp_1 (.A(A[3]), .B(B[3]), .H(n1bit_cmp_1_h), .E(n1bit_cmp_1_e));  // open: L
  _1bit_cmp u_1bit_cmp_2 (.A(A[2]), .B(B[2]), .H(n1bit_cmp_2_h), .E(n1bit_cmp_2_e));  // open: L
  _1bit_cmp u_1bit_cmp_3 (.A(A[1]), .B(B[1]), .H(n1bit_cmp_3_h), .E(n1bit_cmp_3_e));  // open: L
  _1bit_cmp u_1bit_cmp_4 (.A(A[0]), .B(B[0]), .H(n1bit_cmp_4_h));  // open: E, L
  and and_1 (and_1_out, n1bit_cmp_1_e, n1bit_cmp_2_h);
  and and_2 (and_2_out, n1bit_cmp_1_e, n1bit_cmp_2_e, n1bit_cmp_3_h);
  and and_3 (and_3_out, n1bit_cmp_1_e, n1bit_cmp_2_e, n1bit_cmp_3_e, n1bit_cmp_4_h);
  or or_1 (Out, n1bit_cmp_1_h, and_1_out, and_2_out, and_3_out);
endmodule

module Dcmp (
  input  [3:0] A,
  input  [3:0] B,
  output Out
);

  wire and_1_out, and_2_out, and_3_out, n1bit_cmp_1_e, n1bit_cmp_1_l, n1bit_cmp_2_e, n1bit_cmp_2_h,
       n1bit_cmp_3_e, n1bit_cmp_3_h, n1bit_cmp_4_h;

  _1bit_cmp u_1bit_cmp_1 (.A(A[3]), .B(B[3]), .E(n1bit_cmp_1_e), .L(n1bit_cmp_1_l));  // open: H
  _1bit_cmp u_1bit_cmp_2 (.A(A[2]), .B(B[2]), .H(n1bit_cmp_2_h), .E(n1bit_cmp_2_e));  // open: L
  _1bit_cmp u_1bit_cmp_3 (.A(A[1]), .B(B[1]), .H(n1bit_cmp_3_h), .E(n1bit_cmp_3_e));  // open: L
  _1bit_cmp u_1bit_cmp_4 (.A(A[0]), .B(B[0]), .H(n1bit_cmp_4_h));  // open: E, L
  and and_1 (and_1_out, n1bit_cmp_1_e, n1bit_cmp_2_h);
  and and_2 (and_2_out, n1bit_cmp_1_e, n1bit_cmp_2_e, n1bit_cmp_3_h);
  and and_3 (and_3_out, n1bit_cmp_1_e, n1bit_cmp_2_e, n1bit_cmp_3_e, n1bit_cmp_4_h);
  or or_1 (Out, n1bit_cmp_1_l, and_1_out, and_2_out, and_3_out);
endmodule

module bu (
  input  [3:0] in_1,
  output [3:0] out_2
);

  wire [2:0] not_3_out;
  wire [3:0] adder_1_out;

  not not_1 (not_3_out[2], in_1[2]);
  not not_2 (not_3_out[1], in_1[1]);
  not not_3 (not_3_out[0], in_1[0]);
  Adder #(.width(4)) adder_1 (.a({in_1[3], not_3_out}), .b(4'b0001), .out(adder_1_out));  // open: cin, cout
  Multiplexer #(.width(4), .enable("false")) multiplexer_1 (.in0(in_1), .in1(adder_1_out), .out(out_2), .sel(in_1[3]));
endmodule
