// Logisim project ljycompara.circ as structural Verilog: 2 circuits, main circuit 4BIT
module _4BIT (
  input  [3:0] A,
  input  [3:0] B,
  output out_3
);

  wire and_1_out, and_2_out, and_3_out, n1bit_1_e, n1bit_1_h, n1bit_2_h, n1bit_3_e, n1bit_3_l, n1bit_4_e,
       n1bit_4_h;

  _1BIT u_1bit_1 (.A(A[1]), .B(B[1]), .H(n1bit_1_h), .E(n1bit_1_e));  // open: L
  _1BIT u_1bit_2 (.A(A[0]), .B(B[0]), .H(n1bit_2_h));  // open: E, L
  _1BIT u_1bit_3 (.A(A[3]), .B(B[3]), .E(n1bit_3_e), .L(n1bit_3_l));  // open: H
  _1BIT u_1bit_4 (.A(A[2]), .B(B[2]), .H(n1bit_4_h), .E(n1bit_4_e));  // open: L
  and and_1 (and_1_out, n1bit_3_e, n1bit_4_h);
  and and_2 (and_2_out, n1bit_3_e, n1bit_4_e, n1bit_1_h);
  and and_3 (and_3_out, n1bit_2_h, n1bit_3_e, n1bit_4_e, n1bit_1_e);
  or or_1 (out_3, n1bit_3_l, and_1_out, and_2_out, and_3_out);
endmodule

module _1BIT (
  input  A,
  input  B,
  output H,
  output E,
  output L
);

  wire and_2_out, and_3_out, not_1_out, not_2_out, not_3_out, not_4_out;

  not not_1 (not_1_out, B);
  not not_2 (not_2_out, A);
  not not_3 (not_3_out, B);
  not not_4 (not_4_out, A);
  and and_1 (H, A, not_1_out);
  and and_2 (and_2_out, not_2_out, not_3_out);
  and and_3 (and_3_out, A, B);
  and and_4 (L, not_4_out, B);
  or or_1 (E, and_2_out, and_3_out);
endmodule
