// Logisim project 101.circ as structural Verilog: 1 circuit, main circuit fsm
module fsm (
  input  Clr,
  input  X,
  input  in_3,
  input  in_4,
  output out_5,
  output Z,
  output out_7
);

  wire and_1_out, and_2_out, clock_1_out, clock_2_out, clock_3_out, not_1_out, not_2_out, not_3_out,
       not_4_out, not_5_out, or_1_out, S0_q, S1_2_q, S1_3_q, S1_4_q, S1_5_q, S1_6_q, S1_q;

  not not_1 (not_1_out, X);
  not not_2 (not_2_out, S0_q);
  and and_1 (and_1_out, not_1_out, S0_q);
  and and_2 (and_2_out, X, S1_q, not_2_out);
  or or_1 (or_1_out, and_1_out, and_2_out);
  Register #(.width(1)) S1 (.D(or_1_out), .Q(S1_q), .clk(clock_1_out), .clr(Clr));  // open: en
  Register #(.width(1)) S0 (.D(X), .Q(S0_q), .clk(clock_1_out), .clr(Clr));  // open: en
  Clock clock_1 (.out(clock_1_out));
  not not_3 (not_3_out, S0_q);
  and and_3 (Z, X, S1_q, not_3_out);
  Clock clock_2 (.out(clock_2_out));
  Clock clock_3 (.out(clock_3_out));
  Register #(.width(1)) S1_2 (.D(in_3), .Q(S1_2_q), .clk(clock_2_out));  // open: en, clr
  Register #(.width(1)) S1_3 (.D(in_4), .Q(S1_3_q), .clk(clock_3_out));  // open: en, clr
  not not_4 (not_4_out, S1_2_q);
  Register #(.width(1)) S1_4 (.D(S1_2_q), .Q(S1_4_q), .clk(clock_2_out));  // open: en, clr
  Register #(.width(1)) S1_5 (.D(S1_3_q), .Q(S1_5_q), .clk(clock_3_out));  // open: en, clr
  not not_5 (not_5_out, S1_5_q);
  Register #(.width(1)) S1_6 (.D(S1_5_q), .Q(S1_6_q), .clk(clock_3_out));  // open: en, clr
  and and_4 (out_5, in_3, not_4_out, S1_4_q);
  and and_5 (out_7, S1_3_q, not_5_out, S1_6_q);

  // Notes on the sheet:
  //   S0'
endmodule
