// Logisim project P3.circ as structural Verilog: 7 circuits, main circuit ALU
module main (
  input  Reset,
  output [31:0] out_2,
  output out_3,
  output [4:0] out_4,
  output [31:0] out_5,
  output out_6,
  output [4:0] out_7,
  output [31:0] out_8
);

  wire ALUSrc, BEQ, big, bltz, Clk, equal, MemRead, MemReg, RegDst, \small , Zero;
  wire [1:0] EXTOp;
  wire [2:0] ALUOp;
  wire [31:0] alu_1_result, dm_1_read_data, grf_1_read_data1, multiplexer_2_out, offset, shifter_1_out;

  Clock u_clk (.out(Clk));
  IFU ifu_1 (
    .offset(offset), .reset(Reset), .BEQ(BEQ), .read_data(out_2), .zero(Zero), .Clk(Clk), .big(big),
    .\small (\small ), .equal(equal), .bltz(bltz));
  Controller controller_1 (
    .Op(out_2[31:26]), .func(out_2[5:0]), .RegDst(RegDst), .ALUSrc(ALUSrc), .MemtoReg(MemReg),
    .RegWrite(out_3), .MemRead(MemRead), .MemWrite(out_6), .beq(BEQ), .ALUOp(ALUOp), .ExtOp(EXTOp),
    .RT(out_2[20:16]), .bltz(bltz));
  SignEXT signext_1 (.imm(out_2[15:0]), .imm_ex(offset), .EXTOp(EXTOp));
  Multiplexer #(.width(5), .enable("false")) multiplexer_1 (
    .in0(out_2[20:16]), .in1(out_2[15:11]), .out(out_4), .sel(RegDst));
  GRF grf_1 (
    .read_register1(out_2[25:21]), .read_register2(out_2[20:16]), .write_register(out_4), .write_data(out_5),
    .reg_write(out_3), .reset(Reset), .read_data1(grf_1_read_data1), .read_data2(out_8), .Clk(Clk));
  Multiplexer #(.width(32), .enable("false")) multiplexer_2 (
    .in0(out_8), .in1(offset), .out(multiplexer_2_out), .sel(ALUSrc));
  ALU alu_1 (
    .AluOp(ALUOp), .A(grf_1_read_data1), .B(multiplexer_2_out), .zero(Zero), .result(alu_1_result),
    .shamt(out_2[10:6]), .big(big), .\small (\small ), .equal(equal));
  Bit_Extender #(.in_width(32), .out_width(5), .\type ("sign")) bit_extender_1 (.in(shifter_1_out), .out(out_7));
  Shifter #(.width(32), .shift("lr")) shifter_1 (.in(alu_1_result), .\dist (5'b00010), .out(shifter_1_out));
  DM dm_1 (
    .addr(out_7), .writr_data(out_8), .reset(Reset), .read_data(dm_1_read_data), .MemRead(MemRead),
    .MemWrite(out_6), .Clk(Clk));
  Multiplexer #(.width(32), .enable("false")) multiplexer_3 (
    .in0(alu_1_result), .in1(dm_1_read_data), .out(out_5), .sel(MemReg));

  // Other names for the same wires on the sheet: func[5:0] = out_2[5:0]; Instr[31:0] = out_2; MemAddr[4:0] = out_7;
  //   MemData[31:0] = out_8; Memory_Write = out_6; MemWrite = out_6; Op[5:0] = out_2[31:26]; RD[4:0] = out_2[15:11];
  //   RegAddr[4:0] = out_4; Regdata[31:0] = out_5; RegWrite = out_3; RW = out_3; RS[4:0] = out_2[25:21];
  //   RT[4:0] = out_2[20:16]; shamt[4:0] = out_2[10:6]
endmodule

module ALU (
  input  [2:0] AluOp,
  input  [31:0] A,
  input  [31:0] B,
  input  [4:0] shamt,
  output zero,
  output [31:0] result,
  output big,
  output equal,
  output \small 
);

  wire [31:0] adder_1_out, and_out, or_out, shifter_1_out, shifter_2_out, subtractor_1_out;

  Adder #(.width(32)) adder_1 (.a(A), .b(B), .out(adder_1_out));  // open: cin, cout
  Subtractor #(.width(32)) subtractor_1 (.a(A), .b(B), .out(subtractor_1_out));  // open: bin, bout
  assign or_out = A | B;  // OR_Gate or, 32 bits wide
  Comparator #(.width(32)) comparator_1 (.a(A), .b(B), .eq(zero));  // open: gt, lt
  assign and_out = B & A;  // AND_Gate and, 32 bits wide
  Shifter #(.width(32)) shifter_1 (.in(B), .\dist (shamt), .out(shifter_1_out));
  Shifter #(.width(32), .shift("lr")) shifter_2 (.in(B), .\dist (shamt), .out(shifter_2_out));
  Comparator #(.width(32)) comparator_2 (.a(A), .b({32{1'b0}}), .gt(big), .eq(equal), .lt(\small ));
  Multiplexer #(.select(3), .width(32), .enable("false")) multiplexer_1 (
    .in0(adder_1_out), .in1(subtractor_1_out), .in2(or_out), .in3(and_out), .in4(shifter_1_out),
    .in5(shifter_2_out), .out(result), .sel(AluOp));  // open: in6, in7
endmodule

module IFU (
  input  Clk,
  input  [31:0] offset,
  input  reset,
  input  zero,
  input  BEQ,
  input  big,
  input  equal,
  input  \small ,
  input  bltz,
  output [31:0] read_data
);

  wire beq_out, bltz_out, or_1_out;
  wire [4:0] bit_extender_1_out;
  wire [31:0] adder_1_out, adder_2_out, multiplexer_1_out, PC_q, shifter_1_out, shifter_2_out;

  Register #(.width(32)) PC (.D(multiplexer_1_out), .Q(PC_q), .clk(Clk), .clr(reset));  // open: en
  Shifter #(.width(32), .shift("lr")) shifter_1 (.in(PC_q), .\dist (5'b00010), .out(shifter_1_out));
  Bit_Extender #(.in_width(32), .out_width(5)) bit_extender_1 (.in(shifter_1_out), .out(bit_extender_1_out));
  Adder #(.width(32)) adder_1 (.a(PC_q), .b(32'h4), .out(adder_1_out));  // open: cin, cout
  Shifter #(.width(32)) shifter_2 (.in(offset), .\dist (5'b00010), .out(shifter_2_out));
  ROM #(.addrWidth(5), .dataWidth(32)) rom_1 (.addr(bit_extender_1_out), .data(read_data));  // open: sel
  Adder #(.width(32)) adder_2 (.a(adder_1_out), .b(shifter_2_out), .out(adder_2_out));  // open: cin, cout
  Multiplexer #(.width(32), .enable("false")) multiplexer_1 (
    .in0(adder_1_out), .in1(adder_2_out), .out(multiplexer_1_out), .sel(or_1_out));
  or or_1 (or_1_out, beq_out, bltz_out);
  and u_bltz (bltz_out, bltz, \small );
  and u_beq (beq_out, BEQ, zero);

  // Notes on the sheet:
  //   contents of rom_1 (hex, n*v repeats v):
  //   0 3c08fff1 5000000 3c010000 34210001 1014021 0 0 11290000 ac090000 8c0a0000 1000ffff
endmodule

module GRF (
  input  [4:0] read_register1,
  input  [4:0] read_register2,
  input  [4:0] write_register,
  input  [31:0] write_data,
  input  reg_write,
  input  reset,
  input  Clk,
  output [31:0] read_data1,
  output [31:0] read_data2
);

  wire c0, c1, c2, c3, c4, c5, c6, c7, c8, c9, c10, c11, c12, c13, c14, c15, c16, c17, c18, c19, c20, c21,
       c22, c23, c24, c25, c26, c27, c28, c29, c30, c31, decoder_1_out0, decoder_1_out1, decoder_1_out2,
       decoder_1_out3, decoder_1_out4, decoder_1_out5, decoder_1_out6, decoder_1_out7, decoder_1_out8,
       decoder_1_out9, decoder_1_out10, decoder_1_out11, decoder_1_out12, decoder_1_out13, decoder_1_out14,
       decoder_1_out15, decoder_1_out16, decoder_1_out17, decoder_1_out18, decoder_1_out19, decoder_1_out20,
       decoder_1_out21, decoder_1_out22, decoder_1_out23, decoder_1_out24, decoder_1_out25, decoder_1_out26,
       decoder_1_out27, decoder_1_out28, decoder_1_out29, decoder_1_out30, decoder_1_out31;
  wire [31:0] r0, r1, r2, r3, r4, r5, r6, r7, r8, r9, r10, r11, r12, r13, r14, r15, r16, r17, r18, r19, r20,
       r21, r22, r23, r24, r25, r26, r27, r28, r29, r30, r31;

  Register #(.width(32)) _0 (.D(write_data), .en(c0), .Q(r0), .clk(Clk), .clr(1'b1));
  Register #(.width(32)) _2 (.D(write_data), .en(c2), .Q(r2), .clk(Clk), .clr(reset));
  Register #(.width(32)) _4 (.D(write_data), .en(c4), .Q(r4), .clk(Clk), .clr(reset));
  Register #(.width(32)) _6 (.D(write_data), .en(c6), .Q(r6), .clk(Clk), .clr(reset));
  Register #(.width(32)) _8 (.D(write_data), .en(c8), .Q(r8), .clk(Clk), .clr(reset));
  Register #(.width(32)) _10 (.D(write_data), .en(c10), .Q(r10), .clk(Clk), .clr(reset));
  Register #(.width(32)) _12 (.D(write_data), .en(c12), .Q(r12), .clk(Clk), .clr(reset));
  Register #(.width(32)) _14 (.D(write_data), .en(c14), .Q(r14), .clk(Clk), .clr(reset));
  Register #(.width(32)) _16 (.D(write_data), .en(c16), .Q(r16), .clk(Clk), .clr(reset));
  Register #(.width(32)) _18 (.D(write_data), .en(c18), .Q(r18), .clk(Clk), .clr(reset));
  Register #(.width(32)) _20 (.D(write_data), .en(c20), .Q(r20), .clk(Clk), .clr(reset));
  Register #(.width(32)) _22 (.D(write_data), .en(c22), .Q(r22), .clk(Clk), .clr(reset));
  Register #(.width(32)) _24 (.D(write_data), .en(c24), .Q(r24), .clk(Clk), .clr(reset));
  Register #(.width(32)) _26 (.D(write_data), .en(c26), .Q(r26), .clk(Clk), .clr(reset));
  Register #(.width(32)) _28 (.D(write_data), .en(c28), .Q(r28), .clk(Clk), .clr(reset));
  Register #(.width(32)) _30 (.D(write_data), .en(c30), .Q(r30), .clk(Clk), .clr(reset));
  Register #(.width(32)) _1 (.D(write_data), .en(c1), .Q(r1), .clk(Clk), .clr(reset));
  Register #(.width(32)) _3 (.D(write_data), .en(c3), .Q(r3), .clk(Clk), .clr(reset));
  Register #(.width(32)) _5 (.D(write_data), .en(c5), .Q(r5), .clk(Clk), .clr(reset));
  Register #(.width(32)) _7 (.D(write_data), .en(c7), .Q(r7), .clk(Clk), .clr(reset));
  Register #(.width(32)) _9 (.D(write_data), .en(c9), .Q(r9), .clk(Clk), .clr(reset));
  Register #(.width(32)) _11 (.D(write_data), .en(c11), .Q(r11), .clk(Clk), .clr(reset));
  Register #(.width(32)) _13 (.D(write_data), .en(c13), .Q(r13), .clk(Clk), .clr(reset));
  Register #(.width(32)) _15 (.D(write_data), .en(c15), .Q(r15), .clk(Clk), .clr(reset));
  Register #(.width(32)) _17 (.D(write_data), .en(c17), .Q(r17), .clk(Clk), .clr(reset));
  Register #(.width(32)) _19 (.D(write_data), .en(c19), .Q(r19), .clk(Clk), .clr(reset));
  Register #(.width(32)) _21 (.D(write_data), .en(c21), .Q(r21), .clk(Clk), .clr(reset));
  Register #(.width(32)) _23 (.D(write_data), .en(c23), .Q(r23), .clk(Clk), .clr(reset));
  Register #(.width(32)) _25 (.D(write_data), .en(c25), .Q(r25), .clk(Clk), .clr(reset));
  Register #(.width(32)) _27 (.D(write_data), .en(c27), .Q(r27), .clk(Clk), .clr(reset));
  Register #(.width(32)) _29 (.D(write_data), .en(c29), .Q(r29), .clk(Clk), .clr(reset));
  Register #(.width(32)) _31 (.D(write_data), .en(c31), .Q(r31), .clk(Clk), .clr(reset));
  Decoder #(.select(5), .disabled(0)) decoder_1 (
    .out0(decoder_1_out0), .out1(decoder_1_out1), .out2(decoder_1_out2), .out3(decoder_1_out3),
    .out4(decoder_1_out4), .out5(decoder_1_out5), .out6(decoder_1_out6), .out7(decoder_1_out7),
    .out8(decoder_1_out8), .out9(decoder_1_out9), .out10(decoder_1_out10), .out11(decoder_1_out11),
    .out12(decoder_1_out12), .out13(decoder_1_out13), .out14(decoder_1_out14), .out15(decoder_1_out15),
    .out16(decoder_1_out16), .out17(decoder_1_out17), .out18(decoder_1_out18), .out19(decoder_1_out19),
    .out20(decoder_1_out20), .out21(decoder_1_out21), .out22(decoder_1_out22), .out23(decoder_1_out23),
    .out24(decoder_1_out24), .out25(decoder_1_out25), .out26(decoder_1_out26), .out27(decoder_1_out27),
    .out28(decoder_1_out28), .out29(decoder_1_out29), .out30(decoder_1_out30), .out31(decoder_1_out31),
    .sel(write_register), .en(reg_write));
  and and_1 (c0, 1'b1, decoder_1_out0);
  and and_2 (c1, 1'b1, decoder_1_out1);
  and and_3 (c2, 1'b1, decoder_1_out2);
  and and_4 (c3, 1'b1, decoder_1_out3);
  and and_5 (c4, 1'b1, decoder_1_out4);
  and and_6 (c5, 1'b1, decoder_1_out5);
  and and_7 (c6, 1'b1, decoder_1_out6);
  and and_8 (c7, 1'b1, decoder_1_out7);
  and and_9 (c8, 1'b1, decoder_1_out8);
  and and_10 (c9, 1'b1, decoder_1_out9);
  and and_11 (c10, 1'b1, decoder_1_out10);
  and and_12 (c11, 1'b1, decoder_1_out11);
  and and_13 (c12, 1'b1, decoder_1_out12);
  and and_14 (c13, 1'b1, decoder_1_out13);
  and and_15 (c14, 1'b1, decoder_1_out14);
  and and_16 (c15, 1'b1, decoder_1_out15);
  and and_17 (c16, 1'b1, decoder_1_out16);
  and and_18 (c17, 1'b1, decoder_1_out17);
  and and_19 (c18, 1'b1, decoder_1_out18);
  and and_20 (c19, 1'b1, decoder_1_out19);
  and and_21 (c20, 1'b1, decoder_1_out20);
  and and_22 (c21, 1'b1, decoder_1_out21);
  and and_23 (c22, 1'b1, decoder_1_out22);
  and and_24 (c23, 1'b1, decoder_1_out23);
  and and_25 (c24, 1'b1, decoder_1_out24);
  and and_26 (c25, 1'b1, decoder_1_out25);
  and and_27 (c26, 1'b1, decoder_1_out26);
  and and_28 (c27, 1'b1, decoder_1_out27);
  and and_29 (c28, 1'b1, decoder_1_out28);
  and and_30 (c29, 1'b1, decoder_1_out29);
  and and_31 (c30, 1'b1, decoder_1_out30);
  and and_32 (c31, 1'b1, decoder_1_out31);
  Multiplexer #(.select(5), .width(32)) multiplexer_1 (
    .in0(r0), .in1(r1), .in2(r2), .in3(r3), .in4(r4), .in5(r5), .in6(r6), .in7(r7), .in8(r8), .in9(r9),
    .in10(r10), .in11(r11), .in12(r12), .in13(r13), .in14(r14), .in15(r15), .in16(r16), .in17(r17),
    .in18(r18), .in19(r19), .in20(r20), .in21(r21), .in22(r22), .in23(r23), .in24(r24), .in25(r25),
    .in26(r26), .in27(r27), .in28(r28), .in29(r29), .in30(r30), .in31(r31), .out(read_data1),
    .sel(read_register1));  // open: en
  Multiplexer #(.select(5), .width(32)) multiplexer_2 (
    .in0(r0), .in1(r1), .in2(r2), .in3(r3), .in4(r4), .in5(r5), .in6(r6), .in7(r7), .in8(r8), .in9(r9),
    .in10(r10), .in11(r11), .in12(r12), .in13(r13), .in14(r14), .in15(r15), .in16(r16), .in17(r17),
    .in18(r18), .in19(r19), .in20(r20), .in21(r21), .in22(r22), .in23(r23), .in24(r24), .in25(r25),
    .in26(r26), .in27(r27), .in28(r28), .in29(r29), .in30(r30), .in31(r31), .out(read_data2),
    .sel(read_register2));  // open: en

  // Other names for the same wires on the sheet: wd[31:0] = write_data; writer_register[4:0] = write_register
endmodule

module DM (
  input  MemRead,
  input  MemWrite,
  input  [4:0] addr,
  input  [31:0] writr_data,
  input  Clk,
  input  reset,
  output [31:0] read_data
);

  wire undriven;

  RAM #(.addrWidth(5), .dataWidth(32), .bus("separate")) ram_1 (
    .addr(addr), .din(writr_data), .data(read_data), .str(MemWrite), .sel(undriven), .clk(Clk), .ld(MemRead),
    .clr(reset));
endmodule

module Controller (
  input  [4:0] RT,
  input  [5:0] Op,
  input  [5:0] func,
  output RegDst,
  output ALUSrc,
  output MemtoReg,
  output RegWrite,
  output MemRead,
  output MemWrite,
  output beq,
  output [2:0] ALUOp,
  output [1:0] ExtOp,
  output bltz
);

  wire addu, \and , lui, not_1_out, not_2_out, not_3_out, not_4_out, not_5_out, not_6_out, not_7_out,
       not_8_out, not_9_out, not_10_out, not_11_out, not_12_out, not_13_out, not_14_out, not_15_out,
       not_16_out, not_17_out, not_18_out, not_19_out, not_20_out, not_21_out, not_22_out, not_23_out,
       not_24_out, not_25_out, not_26_out, not_27_out, not_28_out, not_29_out, not_30_out, not_31_out,
       not_32_out, not_33_out, not_34_out, not_35_out, not_36_out, not_37_out, not_38_out, not_39_out,
       not_40_out, not_41_out, not_42_out, not_43_out, not_44_out, not_45_out, not_46_out, not_47_out,
       not_48_out, not_49_out, not_50_out, not_51_out, \or , ori, sll, sra, subu;

  not not_1 (not_1_out, Op[5]);
  not not_2 (not_2_out, Op[4]);
  not not_3 (not_3_out, func[2]);
  not not_4 (not_4_out, func[3]);
  not not_5 (not_5_out, func[4]);
  not not_6 (not_6_out, func[1]);
  and u_addu (addu, func[5], not_5_out, not_4_out, not_3_out, not_6_out, func[0], RegDst);
  not not_7 (not_7_out, Op[0]);
  not not_8 (not_8_out, Op[3]);
  not not_9 (not_9_out, Op[2]);
  not not_10 (not_10_out, Op[1]);
  and R_format (RegDst, not_1_out, not_2_out, not_8_out, not_9_out, not_10_out, not_7_out);
  not not_11 (not_11_out, func[3]);
  not not_12 (not_12_out, func[2]);
  not not_13 (not_13_out, func[4]);
  and u_subu (subu, RegDst, func[5], not_13_out, not_11_out, not_12_out, func[1], func[0]);
  not not_14 (not_14_out, func[1]);
  not not_15 (not_15_out, func[3]);
  not not_16 (not_16_out, func[0]);
  not not_17 (not_17_out, func[4]);
  and u_and (\and , RegDst, func[5], not_17_out, not_15_out, func[2], not_14_out, not_16_out);
  not not_18 (not_18_out, func[3]);
  not not_19 (not_19_out, func[4]);
  not not_20 (not_20_out, func[1]);
  and u_or (\or , RegDst, func[5], not_19_out, not_18_out, func[2], not_20_out, func[0]);
  not not_21 (not_21_out, func[4]);
  not not_22 (not_22_out, func[0]);
  not not_23 (not_23_out, func[1]);
  not not_24 (not_24_out, func[3]);
  not not_25 (not_25_out, func[2]);
  not not_26 (not_26_out, func[5]);
  and u_sll (sll, RegDst, not_26_out, not_21_out, not_24_out, not_25_out, not_23_out, not_22_out);
  or u_alusrc (ALUSrc, MemWrite, MemRead, ori, lui);
  buf or_2 (MemtoReg, MemRead);  // OR_Gate
  or rw (RegWrite, MemRead, lui, RegDst, ori);
  or or_3 (ALUOp[0], sra, \and , subu);
  or or_4 (ALUOp[1], ori, \and , \or );
  or or_5 (ALUOp[2], sll, sra);
  buf or_6 (ExtOp[0], lui);  // OR_Gate
  or or_7 (ExtOp[1], bltz, beq);
  not not_27 (not_27_out, func[3]);
  not not_28 (not_28_out, func[2]);
  not not_29 (not_29_out, func[5]);
  not not_30 (not_30_out, func[4]);
  and u_sra (sra, RegDst, not_29_out, not_30_out, not_27_out, not_28_out, func[1], func[0]);
  not not_31 (not_31_out, Op[4]);
  not not_32 (not_32_out, Op[1]);
  not not_33 (not_33_out, Op[5]);
  and u_ori (ori, not_33_out, not_31_out, Op[3], Op[2], not_32_out, Op[0]);
  not not_34 (not_34_out, Op[4]);
  not not_35 (not_35_out, Op[3]);
  and lw (MemRead, Op[5], not_34_out, not_35_out, not_36_out, Op[1], Op[0]);
  not not_36 (not_36_out, Op[2]);
  not not_37 (not_37_out, Op[4]);
  not not_38 (not_38_out, Op[2]);
  and sw (MemWrite, Op[5], not_37_out, Op[3], not_38_out, Op[1], Op[0]);
  not not_39 (not_39_out, Op[5]);
  not not_40 (not_40_out, Op[1]);
  not not_41 (not_41_out, Op[4]);
  not not_42 (not_42_out, Op[3]);
  and u_beq (beq, not_39_out, not_41_out, not_42_out, Op[2], not_40_out, not_43_out);
  not not_43 (not_43_out, Op[0]);
  not not_44 (not_44_out, Op[5]);
  not not_45 (not_45_out, Op[4]);
  and u_lui (lui, not_44_out, not_45_out, Op[3], Op[2], Op[1], Op[0]);
  not not_46 (not_46_out, Op[2]);
  not not_47 (not_47_out, Op[3]);
  not not_48 (not_48_out, Op[1]);
  not not_49 (not_49_out, Op[4]);
  not not_50 (not_50_out, Op[5]);
  and u_bltz (bltz, not_50_out, not_49_out, not_47_out, not_46_out, not_48_out, Op[0], not_51_out);
  not not_51 (not_51_out, RT[0]);

  // Other names for the same wires on the sheet: lw = MemRead; R_format = RegDst; judge = RT[0]; sw = MemWrite
endmodule

module SignEXT (
  input  [15:0] imm,
  input  [1:0] EXTOp,
  output [31:0] imm_ex
);

  wire [31:0] bit_extender_1_out, bit_extender_2_out, shifter_1_out;

  assign bit_extender_1_out = {{16{1'b0}}, imm};  // Bit_Extender bit_extender_1
  assign bit_extender_2_out = {{16{imm[15]}}, imm};  // Bit_Extender bit_extender_2
  Shifter #(.width(32)) shifter_1 (.in(bit_extender_1_out), .\dist (5'b10000), .out(shifter_1_out));
  Multiplexer #(.select(2), .width(32), .enable("false")) multiplexer_1 (
    .in0(bit_extender_1_out), .in1(shifter_1_out), .in2(bit_extender_2_out), .out(imm_ex), .sel(EXTOp));  // open: in3
endmodule
