// Logisim project single_cycle.circ as structural Verilog: 6 circuits, main circuit ALU
module ALU (
  input  [31:0] A,
  input  [31:0] B,
  input  [1:0] ALUOP,
  output ZERO,
  output [31:0] C
);

  wire [31:0] adder_1_out, or_1_out, subtractor_1_out;

  Comparator #(.width(32)) comparator_1 (.a(A), .b(B), .eq(ZERO));  // open: gt, lt
  Adder #(.width(32)) adder_1 (.a(A), .b(B), .out(adder_1_out));  // open: cin, cout
  Subtractor #(.width(32)) subtractor_1 (.a(A), .b(B), .out(subtractor_1_out));  // open: bin, bout
  assign or_1_out = A | B;  // OR_Gate or_1, 32 bits wide
  Multiplexer #(.select(2), .width(32), .enable("false")) multiplexer_1 (
    .in0(adder_1_out), .in1(subtractor_1_out), .in2(or_1_out), .out(C), .sel(ALUOP));  // open: in3
endmodule

module GRF (
  input  Reset,
  input  [31:0] RegData,
  input  Clk,
  input  [4:0] R1,
  input  [4:0] R2,
  input  RegWrite,
  input  [4:0] RegAddr,
  output [31:0] RD1,
  output [31:0] RD2
);

  wire W0, W1, W2, W3, W4, W5, W6, W7, W8, W9, W10, W11, W12, W13, W14, W15, W16, W17, W18, W19, W20, W21,
       W22, W23, W24, W25, W26, W27, W28, W29, W30, W31;
  wire [31:0] _0, _1, _2, _3, _4, _5, _6, _7, _8, _9, _10, _11, _12, _13, _14, _15, _16, _17, _18, _19, _20,
       _21, _22, _23, _24, _25, _26, _27, _28, _29, _30, _31, undriven;

  Decoder #(.select(5), .disabled(0)) decoder_1 (
    .out0(W0), .out1(W1), .out2(W2), .out3(W3), .out4(W4), .out5(W5), .out6(W6), .out7(W7), .out8(W8),
    .out9(W9), .out10(W10), .out11(W11), .out12(W12), .out13(W13), .out14(W14), .out15(W15), .out16(W16),
    .out17(W17), .out18(W18), .out19(W19), .out20(W20), .out21(W21), .out22(W22), .out23(W23), .out24(W24),
    .out25(W25), .out26(W26), .out27(W27), .out28(W28), .out29(W29), .out30(W30), .out31(W31), .sel(RegAddr),
    .en(RegWrite));
  Register #(.width(32)) register_1 (.D(RegData), .en(W0), .Q(_0), .clk(Clk), .clr(1'b1));
  Register #(.width(32)) register_2 (.D(RegData), .en(W1), .Q(_1), .clk(Clk), .clr(Reset));
  Register #(.width(32)) register_3 (.D(RegData), .en(W2), .Q(_2), .clk(Clk), .clr(Reset));
  Register #(.width(32)) register_4 (.D(RegData), .en(W3), .Q(_3), .clk(Clk), .clr(Reset));
  Register #(.width(32)) register_5 (.D(RegData), .en(W4), .Q(_4), .clk(Clk), .clr(Reset));
  Register #(.width(32)) register_6 (.D(RegData), .en(W5), .Q(_5), .clk(Clk), .clr(Reset));
  Register #(.width(32)) register_7 (.D(RegData), .en(W6), .Q(_6), .clk(Clk), .clr(Reset));
  Register #(.width(32)) register_8 (.D(RegData), .en(W7), .Q(_7), .clk(Clk), .clr(Reset));
  Register #(.width(32)) u__8 (.D(RegData), .en(W8), .Q(_8), .clk(Clk), .clr(Reset));
  Register #(.width(32)) register_9 (.D(RegData), .en(W9), .Q(_9), .clk(Clk), .clr(Reset));
  Register #(.width(32)) register_10 (.D(RegData), .en(W10), .Q(_10), .clk(Clk), .clr(Reset));
  Register #(.width(32)) register_11 (.D(RegData), .en(W11), .Q(_11), .clk(Clk), .clr(Reset));
  Register #(.width(32)) register_12 (.D(RegData), .en(W12), .Q(_12), .clk(Clk), .clr(Reset));
  Register #(.width(32)) register_13 (.D(RegData), .en(W13), .Q(_13), .clk(Clk), .clr(Reset));
  Register #(.width(32)) register_14 (.D(RegData), .en(W14), .Q(_14), .clk(Clk), .clr(Reset));
  Register #(.width(32)) register_15 (.D(RegData), .en(W15), .Q(_15), .clk(Clk), .clr(Reset));
  Register #(.width(32)) register_16 (.D(RegData), .en(W16), .Q(_16), .clk(Clk), .clr(Reset));
  Register #(.width(32)) register_17 (.D(RegData), .en(W17), .Q(_17), .clk(Clk), .clr(Reset));
  Register #(.width(32)) register_18 (.D(RegData), .en(W18), .Q(_18), .clk(Clk), .clr(Reset));
  Register #(.width(32)) register_19 (.D(RegData), .en(W19), .Q(_19), .clk(Clk), .clr(Reset));
  Register #(.width(32)) register_20 (.D(RegData), .en(W20), .Q(_20), .clk(Clk), .clr(Reset));
  Register #(.width(32)) register_21 (.D(RegData), .en(W21), .Q(_21), .clk(Clk), .clr(Reset));
  Register #(.width(32)) register_22 (.D(RegData), .en(W22), .Q(_22), .clk(Clk), .clr(Reset));
  Register #(.width(32)) register_23 (.D(RegData), .en(W23), .Q(_23), .clk(Clk), .clr(Reset));
  Register #(.width(32)) register_24 (.D(RegData), .en(W24), .Q(_24), .clk(Clk), .clr(Reset));
  Register #(.width(32)) register_25 (.D(RegData), .en(W25), .Q(_25), .clk(Clk), .clr(Reset));
  Register #(.width(32)) register_26 (.D(RegData), .en(W26), .Q(_26), .clk(Clk), .clr(Reset));
  Register #(.width(32)) register_27 (.D(RegData), .en(W27), .Q(_27), .clk(Clk), .clr(Reset));
  Register #(.width(32)) register_28 (.D(RegData), .en(W28), .Q(_28), .clk(Clk), .clr(Reset));
  Register #(.width(32)) register_29 (.D(RegData), .en(W29), .Q(_29), .clk(Clk), .clr(Reset));
  Register #(.width(32)) register_30 (.D(RegData), .en(W30), .Q(_30), .clk(Clk), .clr(Reset));
  Register #(.width(32)) register_31 (.D(RegData), .en(W31), .Q(_31), .clk(Clk), .clr(Reset));
  Multiplexer #(.select(5), .width(32), .enable("false")) multiplexer_1 (
    .in0(_0), .in1(_1), .in2(_2), .in3(_3), .in4(_4), .in5(_5), .in6(_6), .in7(_7), .in8(_8), .in9(_9),
    .in10(_10), .in11(_11), .in12(_12), .in13(_13), .in14(_14), .in15(_15), .in16(_16), .in17(_17),
    .in18(_18), .in19(_19), .in20(_20), .in21(_21), .in22(_22), .in23(_23), .in24(_24), .in25(_25),
    .in26(_26), .in27(_27), .in28(_28), .in29(_29), .in30(_30), .in31(_31), .out(RD1), .sel(R1));
  Multiplexer #(.select(5), .width(32), .enable("false")) multiplexer_2 (
    .in0(_0), .in1(_1), .in2(_2), .in3(_3), .in4(_4), .in5(undriven), .in6(_6), .in7(_7), .in8(_8), .in9(_9),
    .in10(_10), .in11(_11), .in12(_12), .in13(_13), .in14(_14), .in15(_15), .in16(_16), .in17(_17),
    .in18(_18), .in19(_19), .in20(_20), .in21(_21), .in22(_22), .in23(_23), .in24(_24), .in25(_25),
    .in26(_26), .in27(_27), .in28(_28), .in29(_29), .in30(_30), .in31(_31), .out(RD2), .sel(R2));
endmodule

module EXT (
  input  [15:0] A,
  input  [1:0] ExtOp,
  output [31:0] C
);

  wire [31:0] bit_extender_1_out, bit_extender_2_out, shifter_1_out;

  assign bit_extender_1_out = {{16{1'b0}}, A};  // Bit_Extender bit_extender_1
  assign bit_extender_2_out = {{16{1'b0}}, A};  // Bit_Extender bit_extender_2
  Shifter #(.width(32)) shifter_1 (.in(bit_extender_2_out), .\dist (5'b10000), .out(shifter_1_out));
  Multiplexer #(.select(2), .width(32), .enable("false")) multiplexer_1 (
    .in0(bit_extender_1_out), .in1(shifter_1_out), .in2({{16{1'b1}}, A}), .out(C), .sel(ExtOp));  // open: in3
endmodule

module IFU (
  input  ifbeq,
  input  zero,
  input  Clk,
  input  Reset,
  output [31:0] Instr
);

  wire and_1_out;
  wire [31:0] adder_1_out, adder_2_out, bit_extender_1_out, multiplexer_1_out, register_1_q, shifter_1_out;

  Register #(.width(32)) register_1 (.D(multiplexer_1_out), .Q(register_1_q), .clk(Clk), .clr(Reset));  // open: en
  Adder #(.width(32)) adder_1 (.a(32'h4), .b(register_1_q), .out(adder_1_out));  // open: cin, cout
  ROM #(.addrWidth(5), .dataWidth(32)) rom_1 (.addr(register_1_q[6:2]), .data(Instr));  // open: sel
  assign bit_extender_1_out = {{16{1'b0}}, Instr[15:0]};  // Bit_Extender bit_extender_1
  Shifter #(.width(32)) shifter_1 (.in(bit_extender_1_out), .\dist (5'b00010), .out(shifter_1_out));
  Adder #(.width(32)) adder_2 (.a(adder_1_out), .b(shifter_1_out), .out(adder_2_out));  // open: cin, cout
  Multiplexer #(.width(32), .enable("false")) multiplexer_1 (
    .in0(adder_1_out), .in1(adder_2_out), .out(multiplexer_1_out), .sel(and_1_out));
  and and_1 (and_1_out, ifbeq, zero);

  // Notes on the sheet:
  //   contents of rom_1 (hex, n*v repeats v):
  //   0 3c080001 35080001 1084821 1284823 0 0 0 11290000 ac090000 8c0a0000 1000ffff
endmodule

module Controller (
  input  [5:0] OpCode,
  input  [5:0] Funct,
  output MemRead,
  output RegDst,
  output ALUSrc,
  output MemtoReg,
  output RegWrite,
  output MemWrite,
  output nPC_sel,
  output [1:0] ExtOp,
  output [1:0] ALUOp
);

  wire not_1_out, not_2_out, not_3_out, not_4_out, not_5_out, not_6_out, not_7_out, not_8_out, not_9_out,
       not_10_out, not_11_out, not_12_out, not_13_out, not_14_out, not_15_out, not_16_out, not_17_out,
       not_18_out, not_19_out, not_20_out, not_21_out, not_22_out, not_23_out, not_24_out, not_25_out,
       not_26_out, not_27_out, not_28_out, not_29_out, not_30_out, not_31_out, not_32_out, not_33_out,
       not_34_out, not_35_out, not_36_out, not_37_out, not_38_out, not_39_out, not_40_out;

  not not_1 (not_1_out, OpCode[2]);
  not not_2 (not_2_out, OpCode[1]);
  not not_3 (not_3_out, OpCode[4]);
  not not_4 (not_4_out, OpCode[5]);
  not not_5 (not_5_out, OpCode[0]);
  not not_6 (not_6_out, OpCode[3]);
  and addu_aubu (RegDst, not_4_out, not_3_out, not_6_out, not_1_out, not_2_out, not_5_out);
  not not_7 (not_7_out, OpCode[5]);
  not not_8 (not_8_out, OpCode[2]);
  not not_9 (not_9_out, OpCode[0]);
  not not_10 (not_10_out, OpCode[4]);
  not not_11 (not_11_out, OpCode[1]);
  not not_12 (not_12_out, OpCode[3]);
  not not_13 (not_13_out, Funct[4]);
  not not_14 (not_14_out, Funct[3]);
  not not_15 (not_15_out, Funct[1]);
  not not_16 (not_16_out, Funct[2]);
  // AND_Gate addu has open pins: in0=not_7_out, in1=not_10_out, in2=not_12_out, in3=not_8_out, in4=not_11_out, in5=not_9_out, in7=Funct[5], in8=not_13_out, in9=not_14_out, in10=not_16_out, in11=not_15_out, in12=Funct[0], out=open
  not not_17 (not_17_out, OpCode[2]);
  not not_18 (not_18_out, OpCode[0]);
  not not_19 (not_19_out, OpCode[1]);
  not not_20 (not_20_out, OpCode[5]);
  not not_21 (not_21_out, OpCode[4]);
  not not_22 (not_22_out, OpCode[3]);
  and subu (ALUOp[0], not_20_out, not_21_out, not_22_out, not_17_out, not_19_out, not_18_out, Funct[5], not_23_out, not_24_out, not_25_out, Funct[1], Funct[0]);
  not not_23 (not_23_out, Funct[4]);
  not not_24 (not_24_out, Funct[3]);
  not not_25 (not_25_out, Funct[2]);
  not not_26 (not_26_out, OpCode[5]);
  not not_27 (not_27_out, OpCode[4]);
  not not_28 (not_28_out, OpCode[1]);
  and ori (ALUOp[1], not_26_out, not_27_out, OpCode[3], OpCode[2], not_28_out, OpCode[0]);
  not not_29 (not_29_out, OpCode[4]);
  not not_30 (not_30_out, OpCode[2]);
  not not_31 (not_31_out, OpCode[3]);
  and lw (MemRead, OpCode[5], not_29_out, not_31_out, not_30_out, OpCode[1], OpCode[0]);
  not not_32 (not_32_out, OpCode[2]);
  not not_33 (not_33_out, OpCode[4]);
  and sw (MemWrite, OpCode[5], not_33_out, OpCode[3], not_32_out, OpCode[1], OpCode[0]);
  not not_34 (not_34_out, OpCode[4]);
  not not_35 (not_35_out, OpCode[5]);
  not not_36 (not_36_out, OpCode[3]);
  and beq (ExtOp[1], not_35_out, not_34_out, not_36_out, OpCode[2], not_38_out, not_37_out);
  not not_37 (not_37_out, OpCode[0]);
  not not_38 (not_38_out, OpCode[1]);
  not not_39 (not_39_out, OpCode[5]);
  not not_40 (not_40_out, OpCode[4]);
  and lui (ExtOp[0], not_39_out, not_40_out, OpCode[3], OpCode[2], OpCode[1], OpCode[0]);
  or or_1 (ALUSrc, ALUOp[1], ExtOp[0], MemRead, MemWrite);
  or or_2 (RegWrite, RegDst, ALUOp[1], MemRead, ExtOp[0]);

  assign MemtoReg = MemRead;
  assign nPC_sel = ExtOp[1];
endmodule

module main (
  input  Reset,
  output [31:0] out_2,
  output out_3,
  output [4:0] out_4,
  output [31:0] out_5,
  output out_6,
  output [4:0] out_7,
  output [31:0] out_8
);

  wire ALUSrc, Clk, ifbeq, MemRead, MemtoReg, RegDst, ZERO;
  wire [1:0] ALUOp, extop;
  wire [31:0] ALU_c, EXT_c, multiplexer_3_out, ram_1_data, RD1;

  Clock u_Clk (.out(Clk));
  IFU IFU (.Clk(Clk), .Reset(Reset), .ifbeq(ifbeq), .zero(ZERO), .Instr(out_2));
  Multiplexer #(.width(5), .enable("false")) multiplexer_1 (
    .in0(out_2[20:16]), .in1(out_2[15:11]), .out(out_4), .sel(RegDst));
  Multiplexer #(.width(32), .enable("false")) multiplexer_2 (
    .in0({ALU_c[31:8], out_7, ALU_c[2:0]}), .in1(ram_1_data), .out(out_5), .sel(MemtoReg));
  EXT EXT (.A(out_2[15:0]), .ExtOp(extop), .C(EXT_c));
  GRF grf_1 (
    .Reset(Reset), .RegData(out_5), .Clk(Clk), .R1(out_2[25:21]), .R2(out_2[20:16]), .RegWrite(out_3),
    .RegAddr(out_4), .RD1(RD1), .RD2(out_8));
  Controller controller_1 (
    .OpCode(out_2[31:26]), .Funct(out_2[5:0]), .MemRead(MemRead), .RegDst(RegDst), .ALUSrc(ALUSrc),
    .MemtoReg(MemtoReg), .RegWrite(out_3), .MemWrite(out_6), .nPC_sel(ifbeq), .ExtOp(extop), .ALUOp(ALUOp));
  Multiplexer #(.width(32), .enable("false")) multiplexer_3 (
    .in0(out_8), .in1(EXT_c), .out(multiplexer_3_out), .sel(ALUSrc));
  ALU ALU (.A(RD1), .B(multiplexer_3_out), .ALUOP(ALUOp), .ZERO(ZERO), .C({ALU_c[31:8], out_7, ALU_c[2:0]}));
  RAM #(.addrWidth(5), .dataWidth(32), .bus("separate")) ram_1 (
    .addr(out_7), .din(out_8), .data(ram_1_data), .str(out_6), .clk(Clk), .ld(MemRead));  // open: sel, clr

  // Other names for the same wires on the sheet: funct[5:0] = out_2[5:0]; Instr[31:0] = out_2; MemAddr[4:0] = out_7;
  //   MemWrite = out_6; op[5:0] = out_2[31:26]; R1[4:0] = out_2[25:21]; R2[4:0] = out_2[20:16]; MemData[31:0] = out_8;
  //   RD2[31:0] = out_8; RegAddr[4:0] = out_4; RegData[31:0] = out_5; RegWrite = out_3
endmodule
