// Logisim project 为了p4的cpu.circ as structural Verilog: 7 circuits, main circuit ALU
module main (
  input  Reset,
  output [31:0] out_2,
  output out_3,
  output [4:0] out_4,
  output [31:0] out_5,
  output out_6,
  output [4:0] out_7,
  output [31:0] out_8
);

  wire ALUSrc, Clk, ifbeq, ifbltz, MemRead, MemtoReg, RegDst, \small , zero;
  wire [1:0] EXTOp;
  wire [3:0] ALUOp;
  wire [31:0] extop_1_c, multiplexer_3_out, RD1, ReadData, result;

  Clock u_clk (.out(Clk));
  // Probe on out_2
  IFU ifu_1 (.CLK(Clk), .Reset(Reset), .Instr(out_2), .ifbeq(ifbeq), .zero(zero), .ifbltz(ifbltz), .\small (\small ));
  // Probe on out_2[31:26]
  // Probe on out_2[5:0]
  controller controller_1 (
    .opcode(out_2[31:26]), .func(out_2[5:0]), .ifbeq(ifbeq), .MemRead(MemRead), .MemtoReg(MemtoReg),
    .Extop(EXTOp), .RegDst(RegDst), .MemWrite(out_6), .RegWrite(out_3), .AlUSrc(ALUSrc), .ALUOp(ALUOp[2:0]),
    .ifbltz(ifbltz));
  Multiplexer #(.width(5), .enable("false")) multiplexer_1 (
    .in0(out_2[20:16]), .in1(out_2[15:11]), .out(out_4), .sel(RegDst));
  EXTOp extop_1 (.A(out_2[15:0]), .extop(EXTOp), .C(extop_1_c));
  // Probe on out_5
  Multiplexer #(.width(32), .enable("false")) multiplexer_2 (
    .in0({result[31:7], out_7, result[1:0]}), .in1(ReadData), .out(out_5), .sel(MemtoReg));
  Multiplexer #(.width(32), .enable("false")) multiplexer_3 (
    .in0(out_8), .in1(extop_1_c), .out(multiplexer_3_out), .sel(ALUSrc));
  // Probe on out_4
  ALU alu_1 (
    .A(RD1), .B(multiplexer_3_out), .ALUOp(ALUOp), .ZERO(zero), .ALUOUT({result[31:7], out_7, result[1:0]}));  // open: big, equal, small, left, right
  GRF grf_1 (
    .RegWrite(out_3), .RegAddr(out_4), .R1(out_2[25:21]), .R2(out_2[20:16]), .RD1(RD1), .RD2(out_8),
    .Reset(Reset), .RegData(out_5), .Clk(Clk));
  // Probe on RD1
  // Probe on out_8
  dm dm_1 (
    .MemAddr(out_7), .MemData(out_8), .MemWrite(out_6), .MemRead(MemRead), .ReadData(ReadData),
    .Reset(Reset), .Clk(Clk));
  // Pins of 3 and 4 bits meet at ALUOp

  // Other names for the same wires on the sheet: func[5:0] = out_2[5:0]; Instr[31:0] = out_2; MemAddr[4:0] = out_7;
  //   result[6:2] = out_7; MemWrite = out_6; op[5:0] = out_2[31:26]; R1[4:0] = out_2[25:21]; R2[4:0] = out_2[20:16];
  //   Rd[4:0] = out_2[15:11]; MemData[31:0] = out_8; RD2[31:0] = out_8; RegAddr[4:0] = out_4; RegData[31:0] = out_5;
  //   RegWrite = out_3; ss[4:0] = out_2[10:6]
endmodule

module IFU (
  input  CLK,
  input  ifbeq,
  input  zero,
  input  ifbltz,
  input  \small ,
  input  Reset,
  output [31:0] Instr
);

  wire and_1_out, and_2_out, or_1_out;
  wire [31:0] adder_1_out, adder_2_out, bit_extender_1_out, multiplexer_1_out, register_1_q, shifter_1_out;

  Register #(.width(32)) register_1 (.D(multiplexer_1_out), .Q(register_1_q), .clk(CLK), .clr(Reset));  // open: en
  Adder #(.width(32)) adder_1 (.a(32'h4), .b(register_1_q), .out(adder_1_out));  // open: cin, cout
  ROM #(.addrWidth(5), .dataWidth(32)) rom_1 (.addr(register_1_q[6:2]), .data(Instr));  // open: sel
  assign bit_extender_1_out = {{16{1'b0}}, Instr[15:0]};  // Bit_Extender bit_extender_1
  Shifter #(.width(32)) shifter_1 (.in(bit_extender_1_out), .\dist (5'b00010), .out(shifter_1_out));
  Multiplexer #(.width(32), .enable("false")) multiplexer_1 (
    .in0(adder_1_out), .in1(adder_2_out), .out(multiplexer_1_out), .sel(or_1_out));
  Adder #(.width(32)) adder_2 (.a(adder_1_out), .b(shifter_1_out), .out(adder_2_out));  // open: cin, cout
  or or_1 (or_1_out, and_1_out, and_2_out);
  and and_1 (and_1_out, ifbeq, zero);
  and and_2 (and_2_out, ifbltz, \small );

  // Notes on the sheet:
  //   contents of rom_1 (hex, n*v repeats v):
  //   0 3c08fff1 5000000 3c010000 34210001 1014021 0 0 11290000 ac090000 8c0a0000 1000ffff
endmodule

module ALU (
  input  [31:0] A,
  input  [31:0] B,
  input  [4:0] left,
  input  [4:0] right,
  input  [3:0] ALUOp,
  output ZERO,
  output [31:0] ALUOUT,
  output big,
  output equal,
  output \small 
);

  wire [31:0] adder_1_out, and_out, or_out, shifter_1_out, shifter_2_out, subtractor_1_out;

  Comparator #(.width(32)) comparator_1 (.a(A), .b(B), .eq(ZERO));  // open: gt, lt
  Adder #(.width(32)) adder_1 (.a(A), .b(B), .out(adder_1_out));  // open: cin, cout
  Subtractor #(.width(32)) subtractor_1 (.a(A), .b(B), .out(subtractor_1_out));  // open: bin, bout
  assign or_out = A | B;  // OR_Gate or, 32 bits wide
  assign and_out = A & B;  // AND_Gate and, 32 bits wide
  Shifter #(.width(32)) shifter_1 (.in(B), .\dist (left), .out(shifter_1_out));
  Shifter #(.width(32), .shift("lr")) shifter_2 (.in(B), .\dist (right), .out(shifter_2_out));
  Comparator #(.width(32)) comparator_2 (.a(A), .b({32{1'b0}}), .gt(big), .eq(equal), .lt(\small ));
  Multiplexer #(.select(4), .width(32), .disabled(0), .enable("false")) multiplexer_1 (
    .in4(adder_1_out), .in5(subtractor_1_out), .in6(or_out), .in7(and_out), .in8(shifter_1_out),
    .in9(shifter_2_out), .in10(32'h1), .out(ALUOUT), .sel(ALUOp));  // open: in0, in1, in2, in3, in11, in12, in13, in14, in15
endmodule

module GRF (
  input  RegWrite,
  input  [4:0] RegAddr,
  input  Reset,
  input  [4:0] R1,
  input  [31:0] RegData,
  input  [4:0] R2,
  input  Clk,
  output [31:0] RD1,
  output [31:0] RD2
);

  wire w0, w1, w2, w3, w4, w5, w6, w7, w8, w9, w10, w11, w12, w13, w14, w15, w16, w17, w18, w19, w20, w21,
       w22, w23, w24, w25, w26, w27, w28, w29, w30, w31;
  wire [31:0] _0, _1, _2, _3, _4, _5, _6, _7, _8, _9, _10, _11, _12, _13, _14, _15, _16, _17, _18, _19, _20,
       _21, _22, _23, _24, _25, _26, _27, _28, _29, _30, _31;

  Decoder #(.select(5), .disabled(0)) decoder_1 (
    .out0(w0), .out1(w1), .out2(w2), .out3(w3), .out4(w4), .out5(w5), .out6(w6), .out7(w7), .out8(w8),
    .out9(w9), .out10(w10), .out11(w11), .out12(w12), .out13(w13), .out14(w14), .out15(w15), .out16(w16),
    .out17(w17), .out18(w18), .out19(w19), .out20(w20), .out21(w21), .out22(w22), .out23(w23), .out24(w24),
    .out25(w25), .out26(w26), .out27(w27), .out28(w28), .out29(w29), .out30(w30), .out31(w31), .sel(RegAddr),
    .en(RegWrite));
  Register #(.width(32)) register_1 (.D(RegData), .en(w0), .Q(_0), .clk(Clk), .clr(1'b1));
  Register #(.width(32)) register_2 (.D(RegData), .en(w1), .Q(_1), .clk(Clk), .clr(Reset));
  Register #(.width(32)) register_3 (.D(RegData), .en(w2), .Q(_2), .clk(Clk), .clr(Reset));
  Register #(.width(32)) register_4 (.D(RegData), .en(w3), .Q(_3), .clk(Clk), .clr(Reset));
  Register #(.width(32)) register_5 (.D(RegData), .en(w4), .Q(_4), .clk(Clk), .clr(Reset));
  Register #(.width(32)) register_6 (.D(RegData), .en(w5), .Q(_5), .clk(Clk), .clr(Reset));
  Register #(.width(32)) register_7 (.D(RegData), .en(w6), .Q(_6), .clk(Clk), .clr(Reset));
  Register #(.width(32)) register_8 (.D(RegData), .en(w7), .Q(_7), .clk(Clk), .clr(Reset));
  Register #(.width(32)) register_9 (.D(RegData), .en(w8), .Q(_8), .clk(Clk), .clr(Reset));
  Register #(.width(32)) register_10 (.D(RegData), .en(w9), .Q(_9), .clk(Clk), .clr(Reset));
  Register #(.width(32)) register_11 (.D(RegData), .en(w10), .Q(_10), .clk(Clk), .clr(Reset));
  Register #(.width(32)) register_12 (.D(RegData), .en(w11), .Q(_11), .clk(Clk), .clr(Reset));
  Register #(.width(32)) register_13 (.D(RegData), .en(w12), .Q(_12), .clk(Clk), .clr(Reset));
  Register #(.width(32)) register_14 (.D(RegData), .en(w13), .Q(_13), .clk(Clk), .clr(Reset));
  Register #(.width(32)) register_15 (.D(RegData), .en(w14), .Q(_14), .clk(Clk), .clr(Reset));
  Register #(.width(32)) register_16 (.D(RegData), .en(w15), .Q(_15), .clk(Clk), .clr(Reset));
  Register #(.width(32)) register_17 (.D(RegData), .en(w16), .Q(_16), .clk(Clk), .clr(Reset));
  Register #(.width(32)) register_18 (.D(RegData), .en(w17), .Q(_17), .clk(Clk), .clr(Reset));
  Register #(.width(32)) register_19 (.D(RegData), .en(w18), .Q(_18), .clk(Clk), .clr(Reset));
  Register #(.width(32)) register_20 (.D(RegData), .en(w19), .Q(_19), .clk(Clk), .clr(Reset));
  Register #(.width(32)) register_21 (.D(RegData), .en(w20), .Q(_20), .clk(Clk), .clr(Reset));
  Register #(.width(32)) register_22 (.D(RegData), .en(w21), .Q(_21), .clk(Clk), .clr(Reset));
  Register #(.width(32)) register_23 (.D(RegData), .en(w22), .Q(_22), .clk(Clk), .clr(Reset));
  Register #(.width(32)) register_24 (.D(RegData), .en(w23), .Q(_23), .clk(Clk), .clr(Reset));
  Register #(.width(32)) register_25 (.D(RegData), .en(w24), .Q(_24), .clk(Clk), .clr(Reset));
  Register #(.width(32)) register_26 (.D(RegData), .en(w25), .Q(_25), .clk(Clk), .clr(Reset));
  Register #(.width(32)) register_27 (.D(RegData), .en(w26), .Q(_26), .clk(Clk), .clr(Reset));
  Register #(.width(32)) register_28 (.D(RegData), .en(w27), .Q(_27), .clk(Clk), .clr(Reset));
  Register #(.width(32)) register_29 (.D(RegData), .en(w28), .Q(_28), .clk(Clk), .clr(Reset));
  Register #(.width(32)) register_30 (.D(RegData), .en(w29), .Q(_29), .clk(Clk), .clr(Reset));
  Register #(.width(32)) register_31 (.D(RegData), .en(w30), .Q(_30), .clk(Clk), .clr(Reset));
  Register #(.width(32)) register_32 (.D(RegData), .en(w31), .Q(_31), .clk(Clk), .clr(Reset));
  Multiplexer #(.select(5), .width(32), .enable("false")) multiplexer_1 (
    .in0(_0), .in1(_1), .in2(_2), .in3(_3), .in4(_4), .in5(_5), .in6(_6), .in7(_7), .in8(_8), .in9(_9),
    .in10(_10), .in11(_11), .in12(_12), .in13(_13), .in14(_14), .in15(_15), .in16(_16), .in17(_17),
    .in18(_18), .in19(_19), .in20(_20), .in21(_21), .in22(_22), .in23(_23), .in24(_24), .in25(_25),
    .in26(_26), .in27(_27), .in28(_28), .in29(_29), .in30(_30), .in31(_31), .out(RD1), .sel(R1));
  Multiplexer #(.select(5), .width(32), .enable("false")) multiplexer_2 (
    .in0(_0), .in1(_1), .in2(_2), .in3(_3), .in4(_4), .in5(_5), .in6(_6), .in7(_7), .in8(_8), .in9(_9),
    .in10(_10), .in11(_11), .in12(_12), .in13(_13), .in14(_14), .in15(_15), .in16(_16), .in17(_17),
    .in18(_18), .in19(_19), .in20(_20), .in21(_21), .in22(_22), .in23(_23), .in24(_24), .in25(_25),
    .in26(_26), .in27(_27), .in28(_28), .in29(_29), .in30(_30), .in31(_31), .out(RD2), .sel(R2));
endmodule

module dm (
  input  [4:0] MemAddr,
  input  [31:0] MemData,
  input  MemWrite,
  input  Clk,
  input  MemRead,
  input  Reset,
  output [31:0] ReadData
);

  RAM #(.addrWidth(5), .dataWidth(32), .bus("separate")) ram_1 (
    .addr(MemAddr), .din(MemData), .data(ReadData), .str(MemWrite), .clk(Clk), .ld(MemRead), .clr(Reset));  // open: sel
endmodule

module controller (
  input  [5:0] opcode,
  input  [5:0] func,
  output ifbeq,
  output ifbltz,
  output MemRead,
  output MemtoReg,
  output [1:0] Extop,
  output RegDst,
  output MemWrite,
  output RegWrite,
  output AlUSrc,
  output [2:0] ALUOp
);

  wire and_out, not_1_out, not_2_out, not_3_out, not_4_out, not_5_out, not_6_out, not_7_out, not_8_out,
       not_9_out, not_10_out, not_11_out, not_12_out, not_13_out, not_14_out, not_15_out, not_16_out,
       not_17_out, not_18_out, not_19_out, not_20_out, not_21_out, not_22_out, not_23_out, not_24_out,
       not_25_out, not_26_out, not_27_out, not_28_out, not_29_out, not_30_out, not_31_out, not_32_out,
       not_33_out, not_34_out, not_35_out, not_36_out, not_37_out, not_38_out, not_39_out, not_40_out,
       not_41_out, not_42_out, not_43_out, not_44_out, not_45_out, not_46_out, not_47_out, not_48_out,
       not_49_out, not_50_out, not_51_out, not_52_out, not_53_out, not_54_out, not_55_out, or_out, ORI_out,
       sll_out, sltu_out, sra_out, SUBU_out;

  not not_1 (not_1_out, opcode[1]);
  not not_2 (not_2_out, opcode[2]);
  not not_3 (not_3_out, opcode[4]);
  not not_4 (not_4_out, opcode[0]);
  not not_5 (not_5_out, opcode[3]);
  not not_6 (not_6_out, opcode[5]);
  and R (RegDst, not_6_out, not_3_out, not_5_out, not_2_out, not_1_out, not_4_out);
  not not_7 (not_7_out, func[3]);
  not not_8 (not_8_out, func[4]);
  not not_9 (not_9_out, func[2]);
  not not_10 (not_10_out, func[1]);
  // AND_Gate ADDU has open pins: in0=RegDst, in1=func[5], in2=not_8_out, in3=not_7_out, in4=not_9_out, in5=not_10_out, in6=func[0], out=open
  not not_11 (not_11_out, func[3]);
  not not_12 (not_12_out, func[2]);
  not not_13 (not_13_out, func[4]);
  and SUBU (SUBU_out, func[5], not_13_out, not_11_out, not_12_out, func[1], func[0], RegDst);
  not not_14 (not_14_out, opcode[5]);
  not not_15 (not_15_out, opcode[4]);
  not not_16 (not_16_out, opcode[1]);
  and ORI (ORI_out, not_14_out, not_15_out, opcode[3], opcode[2], not_16_out, opcode[0]);
  not not_17 (not_17_out, opcode[4]);
  not not_18 (not_18_out, opcode[3]);
  not not_19 (not_19_out, opcode[2]);
  and LW (MemRead, opcode[5], not_17_out, not_18_out, not_19_out, opcode[1], opcode[0]);
  not not_20 (not_20_out, opcode[4]);
  not not_21 (not_21_out, opcode[2]);
  and SW (MemWrite, opcode[5], not_20_out, opcode[3], not_21_out, opcode[1], opcode[0]);
  not not_22 (not_22_out, opcode[5]);
  not not_23 (not_23_out, opcode[0]);
  not not_24 (not_24_out, opcode[1]);
  not not_25 (not_25_out, opcode[4]);
  not not_26 (not_26_out, opcode[3]);
  and BEQ (ifbeq, not_22_out, not_25_out, not_26_out, opcode[2], not_24_out, not_23_out);
  not not_27 (not_27_out, opcode[5]);
  not not_28 (not_28_out, opcode[4]);
  and LUI (Extop[0], not_27_out, not_28_out, opcode[3], opcode[2], opcode[1], opcode[0]);
  not not_29 (not_29_out, opcode[4]);
  not not_30 (not_30_out, opcode[3]);
  not not_31 (not_31_out, opcode[1]);
  and \or  (or_out, opcode[5], not_29_out, not_30_out, opcode[2], not_31_out, opcode[0]);
  not not_32 (not_32_out, func[5]);
  not not_33 (not_33_out, func[3]);
  not not_34 (not_34_out, func[1]);
  not not_35 (not_35_out, func[4]);
  not not_36 (not_36_out, func[0]);
  not not_37 (not_37_out, func[2]);
  and sll (sll_out, RegDst, not_32_out, not_35_out, not_33_out, not_37_out, not_34_out, not_36_out);
  not not_38 (not_38_out, func[2]);
  not not_39 (not_39_out, func[3]);
  not not_40 (not_40_out, func[4]);
  not not_41 (not_41_out, func[5]);
  and sra (sra_out, RegDst, not_41_out, not_40_out, not_39_out, not_38_out, func[1], func[0]);
  not not_42 (not_42_out, func[4]);
  not not_43 (not_43_out, func[3]);
  and \and  (and_out, RegDst, func[5], not_42_out, not_43_out, func[2], not_45_out, not_44_out);
  or or_2 (ALUOp[2], sltu_out, sra_out, sll_out);
  not not_44 (not_44_out, func[0]);
  not not_45 (not_45_out, func[1]);
  not not_46 (not_46_out, opcode[5]);
  not not_47 (not_47_out, opcode[4]);
  not not_48 (not_48_out, opcode[1]);
  not not_49 (not_49_out, opcode[2]);
  not not_50 (not_50_out, opcode[3]);
  and bltz (ifbltz, not_46_out, not_47_out, not_50_out, not_49_out, not_48_out, opcode[0]);
  not not_51 (not_51_out, opcode[1]);
  not not_52 (not_52_out, opcode[4]);
  not not_53 (not_53_out, opcode[3]);
  // AND_Gate lhu has open pins: in1=opcode[5], in2=not_52_out, in3=not_53_out, in4=opcode[2], in5=not_51_out, in6=opcode[0], out=open
  or or_3 (Extop[1], ifbltz, ifbeq);
  not not_54 (not_54_out, func[4]);
  not not_55 (not_55_out, func[2]);
  and sltu (sltu_out, RegDst, func[5], not_54_out, func[3], not_55_out, func[1], func[0]);
  or or_4 (ALUOp[1], ORI_out, sltu_out, and_out, or_out);
  or or_5 (ALUOp[0], sra_out, and_out, SUBU_out);
  or or_6 (RegWrite, or_out, RegDst, ORI_out, MemRead, Extop[0]);
  or or_7 (AlUSrc, ifbltz, ORI_out, MemRead, MemWrite, Extop[0]);

  assign MemtoReg = MemRead;
endmodule

module EXTOp (
  input  [15:0] A,
  input  [1:0] extop,
  output [31:0] C
);

  wire [31:0] bit_extender_1_out, bit_extender_2_out;

  assign bit_extender_1_out = {{16{1'b0}}, A};  // Bit_Extender bit_extender_1
  assign bit_extender_2_out = {{16{A[15]}}, A};  // Bit_Extender bit_extender_2
  Multiplexer #(.select(2), .width(32), .enable("false")) multiplexer_1 (
    .in0(bit_extender_1_out), .in1({A, {16{1'b0}}}), .in2(bit_extender_2_out), .out(C), .sel(extop));  // open: in3
endmodule
