// Logisim project 单周期CPU.circ as structural Verilog: 12 circuits, main circuit main
module main (
  input  RESET,
  output [5:0] OPCODE,
  output [5:0] FUNCT
);

  wire alu_1_zero, AluSrc, CLK_out, Mem2Reg, MemWrite, Men2Reg, NPC_SEL, RegDst, RegWrite;
  wire [1:0] ALUOP, EXTOP;
  wire [4:0] multiplexer_1_out;
  wire [25:6] ifu_1_out_5;
  wire [31:0] alu_1_c, data_memory_1_wd, extender_1_extout, multiplexer_2_out, multiplexer_3_out,
       register_file_1_out_8, register_file_1_out_9;

  Clock CLK (.out(CLK_out));
  IFU ifu_1 (.beq(NPC_SEL), .zero(alu_1_zero), .out_5({OPCODE, ifu_1_out_5, FUNCT}), .CLK(CLK_out), .RESET(RESET));
  Controller controller_1 (
    .OPCODE(OPCODE), .funct(FUNCT), .RegDst(RegDst), .ALUSrc(AluSrc), .Mem2Reg(MemWrite),
    .RegWrite(RegWrite), .MemWrite(Men2Reg), .PC_SEL(NPC_SEL), .Exiop(EXTOP), .ALUOP(ALUOP));
  Multiplexer #(.width(5)) multiplexer_1 (
    .in0(ifu_1_out_5[20:16]), .in1(ifu_1_out_5[15:11]), .out(multiplexer_1_out), .sel(RegDst));  // open: en
  register_file register_file_1 (
    .CLK(CLK_out), .WD(multiplexer_2_out), .out_8(register_file_1_out_8), .out_9(register_file_1_out_9),
    .A3(multiplexer_1_out), .WE3(RegWrite), .A1(ifu_1_out_5[25:21]), .A2(ifu_1_out_5[20:16]), .RESET(RESET));
  Extender extender_1 (.Extin({ifu_1_out_5[15:6], FUNCT}), .Extout(extender_1_extout), .ExtOP(EXTOP));
  Multiplexer #(.width(32)) multiplexer_2 (
    .in0(data_memory_1_wd), .in1(alu_1_c), .out(multiplexer_2_out), .sel(Mem2Reg));  // open: en
  Multiplexer #(.width(32)) multiplexer_3 (
    .in0(register_file_1_out_8), .in1(extender_1_extout), .out(multiplexer_3_out), .sel(AluSrc));  // open: en
  ALU alu_1 (.C(alu_1_c), .A(register_file_1_out_9), .B(multiplexer_3_out), .in_3(ALUOP), .zero(alu_1_zero));
  Data_Memory data_memory_1 (
    .RD2(register_file_1_out_8), .in_3(MemWrite), .clk(CLK_out), .RESET(RESET), .WD(data_memory_1_wd),
    .in_1(alu_1_c[31:2]));

  // Notes on the sheet:
  //   EXT
endmodule

module \_1位加法器  (
  input  in_1,
  input  in_2,
  input  in_3,
  output out_4,
  output out_5
);

  wire or_1_out, or_2_out, xnor_1_out, xor_1_out, xor_2_out;

  or or_1 (or_1_out, in_1, in_2, in_3);
  xor xor_1 (xor_1_out, in_1, in_2);
  NotExactlyOne xnor_1 (.out(xnor_1_out), .in0(in_1), .in1(in_2), .in2(in_3));
  xor xor_2 (xor_2_out, xor_1_out, in_3);
  or or_2 (or_2_out, in_1, in_2, in_3);
  and and_1 (out_4, or_1_out, xnor_1_out);
  and and_2 (out_5, xor_2_out, or_2_out);
endmodule

module \_30位加法器  (
  input  [29:0] _1,
  input  [29:0] _2,
  output [29:0] out
);

  wire \n1位加法器_1_out_4 , \n1位加法器_2_out_4 , \n1位加法器_3_out_4 , \n1位加法器_4_out_4 , \n1位加法器_5_out_4 ,
       \n1位加法器_6_out_4 , \n1位加法器_7_out_4 , \n1位加法器_8_out_4 , \n1位加法器_9_out_4 , \n1位加法器_10_out_4 ,
       \n1位加法器_11_out_4 , \n1位加法器_12_out_4 , \n1位加法器_13_out_4 , \n1位加法器_14_out_4 , \n1位加法器_15_out_4 ,
       \n1位加法器_16_out_4 , \n1位加法器_17_out_4 , \n1位加法器_18_out_4 , \n1位加法器_19_out_4 , \n1位加法器_20_out_4 ,
       \n1位加法器_21_out_4 , \n1位加法器_22_out_4 , \n1位加法器_23_out_4 , \n1位加法器_24_out_4 , \n1位加法器_25_out_4 ,
       \n1位加法器_26_out_4 , \n1位加法器_27_out_4 , \n1位加法器_28_out_4 , \n1位加法器_29_out_4 ;

  \_1位加法器  \u_1位加法器_1  (.in_1(_1[0]), .in_2(1'b0), .in_3(_2[0]), .out_4(\n1位加法器_1_out_4 ), .out_5(out[0]));
  \_1位加法器  \u_1位加法器_2  (.in_1(\n1位加法器_1_out_4 ), .in_2(_1[1]), .in_3(_2[1]), .out_4(\n1位加法器_2_out_4 ), .out_5(out[1]));
  \_1位加法器  \u_1位加法器_3  (.in_1(\n1位加法器_2_out_4 ), .in_2(_1[2]), .in_3(_2[2]), .out_4(\n1位加法器_3_out_4 ), .out_5(out[2]));
  \_1位加法器  \u_1位加法器_4  (.in_1(\n1位加法器_3_out_4 ), .in_2(_1[3]), .in_3(_2[3]), .out_4(\n1位加法器_4_out_4 ), .out_5(out[3]));
  \_1位加法器  \u_1位加法器_5  (.in_1(\n1位加法器_4_out_4 ), .in_2(_1[4]), .in_3(_2[4]), .out_4(\n1位加法器_5_out_4 ), .out_5(out[4]));
  \_1位加法器  \u_1位加法器_6  (.in_1(\n1位加法器_5_out_4 ), .in_2(_1[5]), .in_3(_2[5]), .out_4(\n1位加法器_6_out_4 ), .out_5(out[5]));
  \_1位加法器  \u_1位加法器_7  (.in_1(\n1位加法器_6_out_4 ), .in_2(_1[6]), .in_3(_2[6]), .out_4(\n1位加法器_7_out_4 ), .out_5(out[6]));
  \_1位加法器  \u_1位加法器_8  (.in_1(\n1位加法器_7_out_4 ), .in_2(_1[7]), .in_3(_2[7]), .out_4(\n1位加法器_8_out_4 ), .out_5(out[7]));
  \_1位加法器  \u_1位加法器_9  (.in_1(\n1位加法器_8_out_4 ), .in_2(_1[8]), .in_3(_2[8]), .out_4(\n1位加法器_9_out_4 ), .out_5(out[8]));
  \_1位加法器  \u_1位加法器_10  (
    .in_1(\n1位加法器_9_out_4 ), .in_2(_1[9]), .in_3(_2[9]), .out_4(\n1位加法器_10_out_4 ), .out_5(out[9]));
  \_1位加法器  \u_1位加法器_11  (
    .in_1(\n1位加法器_10_out_4 ), .in_2(_1[10]), .in_3(_2[10]), .out_4(\n1位加法器_11_out_4 ), .out_5(out[10]));
  \_1位加法器  \u_1位加法器_12  (
    .in_1(\n1位加法器_11_out_4 ), .in_2(_1[11]), .in_3(_2[11]), .out_4(\n1位加法器_12_out_4 ), .out_5(out[11]));
  \_1位加法器  \u_1位加法器_13  (
    .in_1(\n1位加法器_12_out_4 ), .in_2(_1[12]), .in_3(_2[12]), .out_4(\n1位加法器_13_out_4 ), .out_5(out[12]));
  \_1位加法器  \u_1位加法器_14  (
    .in_1(\n1位加法器_13_out_4 ), .in_2(_1[13]), .in_3(_2[13]), .out_4(\n1位加法器_14_out_4 ), .out_5(out[13]));
  \_1位加法器  \u_1位加法器_15  (
    .in_1(\n1位加法器_14_out_4 ), .in_2(_1[14]), .in_3(_2[14]), .out_4(\n1位加法器_15_out_4 ), .out_5(out[14]));
  \_1位加法器  \u_1位加法器_16  (
    .in_1(\n1位加法器_15_out_4 ), .in_2(_1[15]), .in_3(_2[15]), .out_4(\n1位加法器_16_out_4 ), .out_5(out[15]));
  \_1位加法器  \u_1位加法器_17  (
    .in_1(\n1位加法器_16_out_4 ), .in_2(_1[16]), .in_3(_2[16]), .out_4(\n1位加法器_17_out_4 ), .out_5(out[16]));
  \_1位加法器  \u_1位加法器_18  (
    .in_1(\n1位加法器_17_out_4 ), .in_2(_1[17]), .in_3(_2[17]), .out_4(\n1位加法器_18_out_4 ), .out_5(out[17]));
  \_1位加法器  \u_1位加法器_19  (
    .in_1(\n1位加法器_18_out_4 ), .in_2(_1[18]), .in_3(_2[18]), .out_4(\n1位加法器_19_out_4 ), .out_5(out[18]));
  \_1位加法器  \u_1位加法器_20  (
    .in_1(\n1位加法器_19_out_4 ), .in_2(_1[19]), .in_3(_2[19]), .out_4(\n1位加法器_20_out_4 ), .out_5(out[19]));
  \_1位加法器  \u_1位加法器_21  (
    .in_1(\n1位加法器_20_out_4 ), .in_2(_1[20]), .in_3(_2[20]), .out_4(\n1位加法器_21_out_4 ), .out_5(out[20]));
  \_1位加法器  \u_1位加法器_22  (
    .in_1(\n1位加法器_21_out_4 ), .in_2(_1[21]), .in_3(_2[21]), .out_4(\n1位加法器_22_out_4 ), .out_5(out[21]));
  \_1位加法器  \u_1位加法器_23  (
    .in_1(\n1位加法器_22_out_4 ), .in_2(_1[22]), .in_3(_2[22]), .out_4(\n1位加法器_23_out_4 ), .out_5(out[22]));
  \_1位加法器  \u_1位加法器_24  (
    .in_1(\n1位加法器_23_out_4 ), .in_2(_1[23]), .in_3(_2[23]), .out_4(\n1位加法器_24_out_4 ), .out_5(out[23]));
  \_1位加法器  \u_1位加法器_25  (
    .in_1(\n1位加法器_24_out_4 ), .in_2(_1[24]), .in_3(_2[24]), .out_4(\n1位加法器_25_out_4 ), .out_5(out[24]));
  \_1位加法器  \u_1位加法器_26  (
    .in_1(\n1位加法器_25_out_4 ), .in_2(_1[25]), .in_3(_2[25]), .out_4(\n1位加法器_26_out_4 ), .out_5(out[25]));
  \_1位加法器  \u_1位加法器_27  (
    .in_1(\n1位加法器_26_out_4 ), .in_2(_1[26]), .in_3(_2[26]), .out_4(\n1位加法器_27_out_4 ), .out_5(out[26]));
  \_1位加法器  \u_1位加法器_28  (
    .in_1(\n1位加法器_27_out_4 ), .in_2(_1[27]), .in_3(_2[27]), .out_4(\n1位加法器_28_out_4 ), .out_5(out[27]));
  \_1位加法器  \u_1位加法器_29  (
    .in_1(\n1位加法器_28_out_4 ), .in_2(_1[28]), .in_3(_2[28]), .out_4(\n1位加法器_29_out_4 ), .out_5(out[28]));
  \_1位加法器  \u_1位加法器_30  (.in_1(\n1位加法器_29_out_4 ), .in_2(_1[29]), .in_3(_2[29]), .out_5(out[29]));  // open: out_4
endmodule

module \_32位加法器  (
  input  [31:0] _1,
  input  [31:0] _2,
  output [31:0] out
);

  wire \n1位加法器_1_out_4 , \n1位加法器_2_out_4 , \n1位加法器_3_out_4 , \n1位加法器_4_out_4 , \n1位加法器_5_out_4 ,
       \n1位加法器_6_out_4 , \n1位加法器_7_out_4 , \n1位加法器_8_out_4 , \n1位加法器_9_out_4 , \n1位加法器_10_out_4 ,
       \n1位加法器_11_out_4 , \n1位加法器_12_out_4 , \n1位加法器_13_out_4 , \n1位加法器_14_out_4 , \n1位加法器_15_out_4 ,
       \n1位加法器_16_out_4 , \n1位加法器_17_out_4 , \n1位加法器_18_out_4 , \n1位加法器_19_out_4 , \n1位加法器_20_out_4 ,
       \n1位加法器_21_out_4 , \n1位加法器_22_out_4 , \n1位加法器_23_out_4 , \n1位加法器_24_out_4 , \n1位加法器_25_out_4 ,
       \n1位加法器_26_out_4 , \n1位加法器_27_out_4 , \n1位加法器_28_out_4 , \n1位加法器_29_out_4 , \n1位加法器_30_out_4 ,
       \n1位加法器_31_out_4 ;

  \_1位加法器  \u_1位加法器_1  (.in_1(_1[0]), .in_2(1'b0), .in_3(_2[0]), .out_4(\n1位加法器_1_out_4 ), .out_5(out[0]));
  \_1位加法器  \u_1位加法器_2  (.in_1(\n1位加法器_1_out_4 ), .in_2(_2[1]), .in_3(_1[1]), .out_4(\n1位加法器_2_out_4 ), .out_5(out[1]));
  \_1位加法器  \u_1位加法器_3  (.in_1(\n1位加法器_2_out_4 ), .in_2(_2[2]), .in_3(_1[2]), .out_4(\n1位加法器_3_out_4 ), .out_5(out[2]));
  \_1位加法器  \u_1位加法器_4  (.in_1(\n1位加法器_3_out_4 ), .in_2(_2[3]), .in_3(_1[3]), .out_4(\n1位加法器_4_out_4 ), .out_5(out[3]));
  \_1位加法器  \u_1位加法器_5  (.in_1(\n1位加法器_4_out_4 ), .in_2(_2[4]), .in_3(_1[4]), .out_4(\n1位加法器_5_out_4 ), .out_5(out[4]));
  \_1位加法器  \u_1位加法器_6  (.in_1(\n1位加法器_5_out_4 ), .in_2(_2[5]), .in_3(_1[5]), .out_4(\n1位加法器_6_out_4 ), .out_5(out[5]));
  \_1位加法器  \u_1位加法器_7  (.in_1(\n1位加法器_6_out_4 ), .in_2(_2[6]), .in_3(_1[6]), .out_4(\n1位加法器_7_out_4 ), .out_5(out[6]));
  \_1位加法器  \u_1位加法器_8  (.in_1(\n1位加法器_7_out_4 ), .in_2(_2[7]), .in_3(_1[7]), .out_4(\n1位加法器_8_out_4 ), .out_5(out[7]));
  \_1位加法器  \u_1位加法器_9  (.in_1(\n1位加法器_8_out_4 ), .in_2(_2[8]), .in_3(_1[8]), .out_4(\n1位加法器_9_out_4 ), .out_5(out[8]));
  \_1位加法器  \u_1位加法器_10  (
    .in_1(\n1位加法器_9_out_4 ), .in_2(_2[9]), .in_3(_1[9]), .out_4(\n1位加法器_10_out_4 ), .out_5(out[9]));
  \_1位加法器  \u_1位加法器_11  (
    .in_1(\n1位加法器_10_out_4 ), .in_2(_2[10]), .in_3(_1[10]), .out_4(\n1位加法器_11_out_4 ), .out_5(out[10]));
  \_1位加法器  \u_1位加法器_12  (
    .in_1(\n1位加法器_11_out_4 ), .in_2(_2[11]), .in_3(_1[11]), .out_4(\n1位加法器_12_out_4 ), .out_5(out[11]));
  \_1位加法器  \u_1位加法器_13  (
    .in_1(\n1位加法器_12_out_4 ), .in_2(_2[12]), .in_3(_1[12]), .out_4(\n1位加法器_13_out_4 ), .out_5(out[12]));
  \_1位加法器  \u_1位加法器_14  (
    .in_1(\n1位加法器_13_out_4 ), .in_2(_2[13]), .in_3(_1[13]), .out_4(\n1位加法器_14_out_4 ), .out_5(out[13]));
  \_1位加法器  \u_1位加法器_15  (
    .in_1(\n1位加法器_14_out_4 ), .in_2(_2[14]), .in_3(_1[14]), .out_4(\n1位加法器_15_out_4 ), .out_5(out[14]));
  \_1位加法器  \u_1位加法器_16  (
    .in_1(\n1位加法器_15_out_4 ), .in_2(_2[15]), .in_3(_1[15]), .out_4(\n1位加法器_16_out_4 ), .out_5(out[15]));
  \_1位加法器  \u_1位加法器_17  (
    .in_1(\n1位加法器_16_out_4 ), .in_2(_2[16]), .in_3(_1[16]), .out_4(\n1位加法器_17_out_4 ), .out_5(out[16]));
  \_1位加法器  \u_1位加法器_18  (
    .in_1(\n1位加法器_17_out_4 ), .in_2(_2[17]), .in_3(_1[17]), .out_4(\n1位加法器_18_out_4 ), .out_5(out[17]));
  \_1位加法器  \u_1位加法器_19  (
    .in_1(\n1位加法器_18_out_4 ), .in_2(_2[18]), .in_3(_1[18]), .out_4(\n1位加法器_19_out_4 ), .out_5(out[18]));
  \_1位加法器  \u_1位加法器_20  (
    .in_1(\n1位加法器_19_out_4 ), .in_2(_2[19]), .in_3(_1[19]), .out_4(\n1位加法器_20_out_4 ), .out_5(out[19]));
  \_1位加法器  \u_1位加法器_21  (
    .in_1(\n1位加法器_20_out_4 ), .in_2(_2[20]), .in_3(_1[20]), .out_4(\n1位加法器_21_out_4 ), .out_5(out[20]));
  \_1位加法器  \u_1位加法器_22  (
    .in_1(\n1位加法器_21_out_4 ), .in_2(_2[21]), .in_3(_1[21]), .out_4(\n1位加法器_22_out_4 ), .out_5(out[21]));
  \_1位加法器  \u_1位加法器_23  (
    .in_1(\n1位加法器_22_out_4 ), .in_2(_2[22]), .in_3(_1[22]), .out_4(\n1位加法器_23_out_4 ), .out_5(out[22]));
  \_1位加法器  \u_1位加法器_24  (
    .in_1(\n1位加法器_23_out_4 ), .in_2(_2[23]), .in_3(_1[23]), .out_4(\n1位加法器_24_out_4 ), .out_5(out[23]));
  \_1位加法器  \u_1位加法器_25  (
    .in_1(\n1位加法器_24_out_4 ), .in_2(_2[24]), .in_3(_1[24]), .out_4(\n1位加法器_25_out_4 ), .out_5(out[24]));
  \_1位加法器  \u_1位加法器_26  (
    .in_1(\n1位加法器_25_out_4 ), .in_2(_2[25]), .in_3(_1[25]), .out_4(\n1位加法器_26_out_4 ), .out_5(out[25]));
  \_1位加法器  \u_1位加法器_27  (
    .in_1(\n1位加法器_26_out_4 ), .in_2(_2[26]), .in_3(_1[26]), .out_4(\n1位加法器_27_out_4 ), .out_5(out[26]));
  \_1位加法器  \u_1位加法器_28  (
    .in_1(\n1位加法器_27_out_4 ), .in_2(_2[27]), .in_3(_1[27]), .out_4(\n1位加法器_28_out_4 ), .out_5(out[27]));
  \_1位加法器  \u_1位加法器_29  (
    .in_1(\n1位加法器_28_out_4 ), .in_2(_2[28]), .in_3(_1[28]), .out_4(\n1位加法器_29_out_4 ), .out_5(out[28]));
  \_1位加法器  \u_1位加法器_30  (
    .in_1(\n1位加法器_29_out_4 ), .in_2(_2[29]), .in_3(_1[29]), .out_4(\n1位加法器_30_out_4 ), .out_5(out[29]));
  \_1位加法器  \u_1位加法器_31  (
    .in_1(\n1位加法器_30_out_4 ), .in_2(_2[30]), .in_3(_1[30]), .out_4(\n1位加法器_31_out_4 ), .out_5(out[30]));
  \_1位加法器  \u_1位加法器_32  (.in_1(\n1位加法器_31_out_4 ), .in_2(_2[31]), .in_3(_1[31]), .out_5(out[31]));  // open: out_4
endmodule

module \_32位减法器  (
  input  [31:0] beijian,
  input  [31:0] jian,
  output [31:0] out
);

  wire [31:0] \n32位加法器_1_out , not_1_out;

  assign not_1_out = ~jian;  // NOT_Gate not_1, 32 bits wide
  \_32位加法器  \u_32位加法器_1  (._1(not_1_out), ._2(32'h1), .out(\n32位加法器_1_out ));
  \_32位加法器  \u_32位加法器_2  (._1(beijian), ._2(\n32位加法器_1_out ), .out(out));
endmodule

module \_32位或  (
  input  [31:0] in_1,
  input  [31:0] in_2,
  output [31:0] out_3
);

  assign out_3 = in_1 | in_2;  // OR_Gate or_1, 32 bits wide
endmodule

module IFU (
  input  CLK,
  input  RESET,
  input  beq,
  input  zero,
  output [31:0] out_5
);

  wire and_1_out;
  wire [4:0] PC_q;
  wire [24:0] PC_q_2;
  wire [29:0] bit_extender_1_out, multiplexer_1_out, \n30位加法器_1_out , \n30位加法器_2_out , \n30位加法器_3_out ;

  assign bit_extender_1_out = {{14{1'b0}}, out_5[15:0]};  // Bit_Extender bit_extender_1
  \_30位加法器  \u_30位加法器_1  (._1({PC_q_2, PC_q}), ._2(30'h1), .out(\n30位加法器_1_out ));
  \_30位加法器  \u_30位加法器_2  (._1(bit_extender_1_out), ._2({PC_q_2, PC_q}), .out(\n30位加法器_2_out ));
  \_30位加法器  \u_30位加法器_3  (._1(\n30位加法器_2_out ), ._2(30'h1), .out(\n30位加法器_3_out ));
  and and_1 (and_1_out, beq, zero);
  Multiplexer #(.width(30)) multiplexer_1 (
    .in0(\n30位加法器_1_out ), .in1(\n30位加法器_3_out ), .out(multiplexer_1_out), .sel(and_1_out));  // open: en
  Register #(.width(30)) PC (.D(multiplexer_1_out), .Q({PC_q_2, PC_q}), .clk(CLK), .clr(RESET));  // open: en
  ROM #(.addrWidth(5), .dataWidth(32)) rom_1 (.addr(PC_q), .data(out_5));  // open: sel

  // Notes on the sheet:
  //   contents of rom_1 (hex, n*v repeats v):
  //   7*0 11111111
endmodule

module register_file (
  input  RESET,
  input  CLK,
  input  [31:0] WD,
  input  [4:0] A3,
  input  WE3,
  input  [4:0] A2,
  input  [4:0] A1,
  output [31:0] out_8,
  output [31:0] out_9
);

  wire _00, _24, _25, _26, _27, _28, _29, _30, _31, not_1_out, not_2_out, not_3_out, not_4_out, not_5_out;
  wire [31:0] _00_prime, _01_prime, _02_prime, _03_prime, _04_prime, _05_prime, _06_prime, _07_prime,
       _08_prime, _09_prime, _10_prime, _11_prime, _12_prime, _13_prime, _14_prime, _15_prime, _16_prime,
       _17_prime, _18_prime, _19_prime, _20_prime, _21_prime, _22_prime, _23_prime, _24_prime, _25_prime,
       _26_prime, _27_prime, _28_prime, _29_prime, _30_prime, _31_prime;

  not not_1 (not_1_out, A3[4]);
  not not_2 (not_2_out, A3[3]);
  not not_3 (not_3_out, A3[2]);
  not not_4 (not_4_out, A3[0]);
  not not_5 (not_5_out, A3[1]);
  Register #(.width(32)) u__00 (.D(WD), .Q(_00_prime), .clk(CLK), .clr(RESET));  // open: en
  Register #(.width(32)) _08 (.D(WD), .en(RESET), .Q(_08_prime), .clk(CLK), .clr(RESET));
  Register #(.width(32)) _16 (.D(WD), .en(RESET), .Q(_16_prime), .clk(CLK), .clr(RESET));
  Register #(.width(32)) u__24 (.D(WD), .en(_24), .Q(_24_prime), .clk(CLK), .clr(RESET));
  and and_1 (RESET, WE3, A3[0], not_5_out, not_2_out, not_1_out, not_3_out);
  and and_2 (RESET, WE3, not_4_out, A3[1], not_3_out, not_2_out, not_1_out);
  and and_3 (RESET, WE3, A3[0], A3[1], not_3_out, not_1_out, not_2_out);
  and and_4 (RESET, WE3, not_4_out, not_5_out, A3[2], not_2_out, not_1_out);
  and and_5 (RESET, WE3, A3[0], not_5_out, A3[2], not_2_out, not_1_out);
  and and_6 (RESET, WE3, not_4_out, A3[1], A3[2], not_2_out, not_1_out);
  and and_7 (RESET, WE3, A3[0], A3[1], A3[2], not_2_out, not_1_out);
  and and_8 (RESET, WE3, not_4_out, not_5_out, not_3_out, A3[3], not_1_out);
  and and_9 (RESET, WE3, A3[0], not_5_out, not_3_out, A3[3], not_1_out);
  and and_10 (RESET, WE3, not_4_out, A3[1], not_3_out, A3[3], not_1_out);
  and and_11 (RESET, WE3, A3[0], A3[1], not_3_out, A3[3], not_1_out);
  and and_12 (RESET, WE3, not_4_out, not_5_out, A3[2], A3[3], not_1_out);
  and and_13 (RESET, WE3, A3[0], not_5_out, A3[2], A3[3], not_1_out);
  and and_14 (RESET, WE3, not_4_out, A3[1], A3[2], A3[3], not_1_out);
  and and_15 (RESET, WE3, A3[0], A3[1], A3[2], A3[3], not_1_out);
  and and_16 (_00, WE3, not_4_out, not_5_out, not_3_out, not_2_out, not_1_out);
  and and_17 (RESET, WE3, A3[0], not_5_out, not_2_out, A3[4], not_3_out);
  and and_18 (RESET, WE3, not_4_out, A3[1], not_3_out, not_2_out, A3[4]);
  and and_19 (RESET, WE3, A3[0], A3[1], not_3_out, A3[4], not_2_out);
  and and_20 (RESET, WE3, not_4_out, not_5_out, A3[2], not_2_out, A3[4]);
  and and_21 (RESET, WE3, A3[0], not_5_out, A3[2], not_2_out, A3[4]);
  and and_22 (RESET, WE3, not_4_out, A3[1], A3[2], not_2_out, A3[4]);
  and and_23 (RESET, WE3, A3[0], A3[1], A3[2], not_2_out, A3[4]);
  and and_24 (_24, WE3, not_4_out, not_5_out, not_3_out, A3[3], A3[4]);
  and and_25 (_25, WE3, A3[0], not_5_out, not_3_out, A3[3], A3[4]);
  and and_26 (_26, WE3, not_4_out, A3[1], not_3_out, A3[3], A3[4]);
  and and_27 (_27, WE3, A3[0], A3[1], not_3_out, A3[3], A3[4]);
  and and_28 (_28, WE3, not_4_out, not_5_out, A3[2], A3[3], A3[4]);
  and and_29 (_29, WE3, A3[0], not_5_out, A3[2], A3[3], A3[4]);
  and and_30 (_30, WE3, not_4_out, A3[1], A3[2], A3[3], A3[4]);
  and and_31 (_31, WE3, A3[0], A3[1], A3[2], A3[3], A3[4]);
  and and_32 (RESET, WE3, not_4_out, not_5_out, not_3_out, not_2_out, A3[4]);
  Register #(.width(32)) _01 (.D(WD), .en(RESET), .Q(_01_prime), .clk(CLK), .clr(RESET));
  Register #(.width(32)) _09 (.D(WD), .en(RESET), .Q(_09_prime), .clk(CLK), .clr(RESET));
  Register #(.width(32)) _17 (.D(WD), .en(RESET), .Q(_17_prime), .clk(CLK), .clr(RESET));
  Register #(.width(32)) u__25 (.D(WD), .en(_25), .Q(_25_prime), .clk(CLK), .clr(RESET));
  Register #(.width(32)) _02 (.D(WD), .en(RESET), .Q(_02_prime), .clk(CLK), .clr(RESET));
  Register #(.width(32)) _10 (.D(WD), .en(RESET), .Q(_10_prime), .clk(CLK), .clr(RESET));
  Register #(.width(32)) _18 (.D(WD), .en(RESET), .Q(_18_prime), .clk(CLK), .clr(RESET));
  Register #(.width(32)) u__26 (.D(WD), .en(_26), .Q(_26_prime), .clk(CLK), .clr(RESET));
  Register #(.width(32)) _03 (.D(WD), .en(RESET), .Q(_03_prime), .clk(CLK), .clr(RESET));
  Register #(.width(32)) _11 (.D(WD), .en(RESET), .Q(_11_prime), .clk(CLK), .clr(RESET));
  Register #(.width(32)) _19 (.D(WD), .en(RESET), .Q(_19_prime), .clk(CLK), .clr(RESET));
  Register #(.width(32)) u__27 (.D(WD), .en(_27), .Q(_27_prime), .clk(CLK), .clr(RESET));
  Multiplexer #(.select(5), .width(32)) multiplexer_1 (
    .in0(_00_prime), .in1(_01_prime), .in2(_02_prime), .in3(_03_prime), .in4(_04_prime), .in5(_05_prime),
    .in6(_06_prime), .in7(_07_prime), .in8(_08_prime), .in9(_09_prime), .in10(_10_prime), .in11(_11_prime),
    .in12(_12_prime), .in13(_13_prime), .in14(_14_prime), .in15(_15_prime), .in16(_16_prime),
    .in17(_17_prime), .in18(_18_prime), .in19(_19_prime), .in20(_20_prime), .in21(_21_prime),
    .in22(_22_prime), .in23(_23_prime), .in24(_24_prime), .in25(_25_prime), .in26(_26_prime),
    .in27(_27_prime), .in28(_28_prime), .in29(_29_prime), .in30(_30_prime), .in31(_31_prime), .out(out_9),
    .sel(A1));  // open: en
  Register #(.width(32)) _04 (.D(WD), .en(RESET), .Q(_04_prime), .clk(CLK), .clr(RESET));
  Register #(.width(32)) _12 (.D(WD), .en(RESET), .Q(_12_prime), .clk(CLK), .clr(RESET));
  Register #(.width(32)) _20 (.D(WD), .en(RESET), .Q(_20_prime), .clk(CLK), .clr(RESET));
  Register #(.width(32)) u__28 (.D(WD), .en(_28), .Q(_28_prime), .clk(CLK), .clr(RESET));
  Register #(.width(32)) _05 (.D(WD), .en(RESET), .Q(_05_prime), .clk(CLK), .clr(RESET));
  Register #(.width(32)) _13 (.D(WD), .en(RESET), .Q(_13_prime), .clk(CLK), .clr(RESET));
  Register #(.width(32)) _21 (.D(WD), .en(RESET), .Q(_21_prime), .clk(CLK), .clr(RESET));
  Register #(.width(32)) u__29 (.D(WD), .en(_29), .Q(_29_prime), .clk(CLK), .clr(RESET));
  Multiplexer #(.select(5), .width(32)) multiplexer_2 (
    .in0(_00_prime), .in1(_01_prime), .in2(_02_prime), .in3(_03_prime), .in4(_04_prime), .in5(_05_prime),
    .in6(_06_prime), .in7(_07_prime), .in8(_08_prime), .in9(_09_prime), .in10(_10_prime), .in11(_11_prime),
    .in12(_12_prime), .in13(_13_prime), .in14(_14_prime), .in15(_15_prime), .in16(_16_prime),
    .in17(_17_prime), .in18(_18_prime), .in19(_19_prime), .in20(_20_prime), .in21(_21_prime),
    .in22(_22_prime), .in23(_23_prime), .in24(_24_prime), .in25(_25_prime), .in26(_26_prime),
    .in27(_27_prime), .in28(_28_prime), .in29(_29_prime), .in30(_30_prime), .in31(_31_prime), .out(out_8),
    .sel(A2));  // open: en
  Register #(.width(32)) _06 (.D(WD), .en(RESET), .Q(_06_prime), .clk(CLK), .clr(RESET));
  Register #(.width(32)) _14 (.D(WD), .en(RESET), .Q(_14_prime), .clk(CLK), .clr(RESET));
  Register #(.width(32)) _22 (.D(WD), .en(RESET), .Q(_22_prime), .clk(CLK), .clr(RESET));
  Register #(.width(32)) u__30 (.D(WD), .en(_30), .Q(_30_prime), .clk(CLK), .clr(RESET));
  Register #(.width(32)) _07 (.D(WD), .en(RESET), .Q(_07_prime), .clk(CLK), .clr(RESET));
  Register #(.width(32)) _15 (.D(WD), .en(RESET), .Q(_15_prime), .clk(CLK), .clr(RESET));
  Register #(.width(32)) _23 (.D(WD), .en(RESET), .Q(_23_prime), .clk(CLK), .clr(RESET));
  Register #(.width(32)) u__31 (.D(WD), .en(_31), .Q(_31_prime), .clk(CLK), .clr(RESET));

  // Other names for the same wires on the sheet: _01 = RESET; _02 = RESET; _03 = RESET; _04 = RESET; _05 = RESET;
  //   _06 = RESET; _07 = RESET; _08 = RESET; _09 = RESET; _10 = RESET; _11 = RESET; _12 = RESET; _13 = RESET;
  //   _14 = RESET; _15 = RESET; _16 = RESET; _17 = RESET; _18 = RESET; _19 = RESET; _20 = RESET; _21 = RESET;
  //   _22 = RESET; _23 = RESET
endmodule

module ALU (
  input  [31:0] A,
  input  [31:0] B,
  input  [1:0] in_3,
  output [31:0] C,
  output zero
);

  wire [31:0] addu_out, ori_out_3, subu_out;

  \_32位加法器  addu (._1(B), ._2(A), .out(addu_out));
  \_32位减法器  subu (.beijian(B), .jian(A), .out(subu_out));
  \_32位或  ori (.in_1(B), .in_2(A), .out_3(ori_out_3));
  nor nor_1 (zero, C[0], C[1], C[2], C[3], C[4], C[5], C[6], C[7], C[8], C[9], C[10], C[11], C[12], C[13], C[14], C[15], C[17], C[18], C[19], C[20], C[21], C[22], C[23], C[24], C[25], C[26], C[27], C[28], C[29], C[30], C[31], C[16]);
  // XOR_Gate xor_1 is placed but not wired
  Multiplexer #(.select(2), .width(32)) multiplexer_1 (
    .in0(addu_out), .in1(subu_out), .in2(ori_out_3), .out(C), .sel(in_3));  // open: in3, en
endmodule

module Extender (
  input  [15:0] Extin,
  input  [1:0] ExtOP,
  output [31:0] Extout
);

  Multiplexer #(.select(2), .width(32)) multiplexer_1 (
    .in0({{17{Extin[15]}}, Extin[14:0]}), .in1({{16{1'b0}}, Extin}), .in2({Extin, {16{1'b0}}}), .out(Extout),
    .sel(ExtOP));  // open: in3, en
endmodule

module Controller (
  input  [5:0] OPCODE,
  input  [5:0] funct,
  output RegDst,
  output ALUSrc,
  output Mem2Reg,
  output RegWrite,
  output MemWrite,
  output PC_SEL,
  output [1:0] Exiop,
  output [1:0] ALUOP
);

  wire addu_out, bgtz_out, lw_out, not_1_out, not_2_out, not_3_out, not_4_out, not_5_out, not_6_out,
       not_7_out, not_8_out, not_9_out, not_10_out, not_11_out, not_12_out, subu_out;

  not not_1 (not_1_out, OPCODE[5]);
  not not_2 (not_2_out, OPCODE[4]);
  not not_3 (not_3_out, OPCODE[3]);
  not not_4 (not_4_out, OPCODE[0]);
  not not_5 (not_5_out, OPCODE[2]);
  not not_6 (not_6_out, OPCODE[1]);
  not not_7 (not_7_out, funct[5]);
  not not_8 (not_8_out, funct[1]);
  not not_9 (not_9_out, funct[4]);
  not not_10 (not_10_out, funct[3]);
  not not_11 (not_11_out, funct[2]);
  not not_12 (not_12_out, funct[0]);
  and addu (addu_out, not_4_out, not_6_out, not_5_out, not_3_out, not_2_out, not_1_out, not_9_out, not_10_out, not_11_out, not_8_out, funct[0], funct[5]);
  and subu (subu_out, not_4_out, not_6_out, not_5_out, not_3_out, not_2_out, not_1_out, funct[5], not_9_out, not_10_out, not_11_out, funct[1], funct[0]);
  and ori (ALUOP[1], not_1_out, not_2_out, OPCODE[3], OPCODE[2], not_6_out, OPCODE[0]);
  and lw (lw_out, OPCODE[5], not_2_out, not_3_out, not_5_out, not_6_out, OPCODE[0]);
  and sw (MemWrite, OPCODE[5], not_2_out, OPCODE[3], not_5_out, OPCODE[1], OPCODE[0]);
  and beq (PC_SEL, not_1_out, not_2_out, not_3_out, OPCODE[2], not_6_out, not_4_out);
  and lui (Exiop[1], not_1_out, not_2_out, OPCODE[3], OPCODE[2], OPCODE[1], OPCODE[0]);
  and bgtz (bgtz_out, not_1_out, not_2_out, not_3_out, OPCODE[3], OPCODE[2], OPCODE[1]);
  or u_RegDst (RegDst, addu_out, subu_out);
  or u_ALUSrc (ALUSrc, ALUOP[1], lw_out, MemWrite, Exiop[1]);
  or u_RegWrite (RegWrite, addu_out, subu_out, ALUOP[1], lw_out, Exiop[1]);
  or or_1 (Exiop[0], lw_out, MemWrite);
  or or_2 (ALUOP[0], subu_out, PC_SEL);

  assign Mem2Reg = ALUOP[1];
endmodule

module Data_Memory (
  input  [29:0] in_1,
  input  [31:0] RD2,
  input  in_3,
  input  clk,
  input  RESET,
  output [31:0] WD
);

  RAM #(.addrWidth(5), .dataWidth(32), .bus("separate")) ram_1 (
    .addr(in_1[4:0]), .din(RD2), .data(WD), .str(in_3), .clk(clk), .clr(RESET));  // open: sel, ld
endmodule
